// Logisim project 16 Bit ALU.circ as structural Verilog: 12 circuits, main circuit main
module main (
  input  Cin,
  input  [15:0] A,
  input  [15:0] B,
  input  [15:0] Immideate,
  input  [3:0] OP_Code,
  input  in_6,
  input  in_7,
  input  in_8,
  input  in_9,
  input  [2:0] Address,
  input  [2:0] in_11,
  input  [2:0] in_12,
  output Cout,
  output Cout_Sub,
  output [15:0] Output,
  output BEQ,
  output out_17
);

  wire CLK_out, clock_1_out, clock_2_out;
  wire [15:0] adder_1_out, adder_2_out, adder_3_out, and_1_out, and_2_out, beq_1_output, not_1_out,
       not_2_out, or_1_out, or_2_out, or_3_out, register_1_data01, shift_left_logical_1_output,
       shift_right_logical_1_output, xor_1_out;

  Clock clock_1 (.out(clock_1_out));
  Clock clock_2 (.out(clock_2_out));
  Clock CLK (.out(CLK_out));
  assign not_1_out = ~B;  // NOT_Gate not_1, 16 bits wide
  Adder #(.width(16)) adder_1 (.a(A), .b(B), .out(adder_1_out), .cin(Cin), .cout(Cout));
  Adder #(.width(16)) adder_2 (.a(A), .b(not_1_out), .out(adder_2_out), .cin(1'b1), .cout(Cout_Sub));
  assign or_1_out = A | B;  // OR_Gate or_1, 16 bits wide
  assign and_1_out = A & B;  // AND_Gate and_1, 16 bits wide
  assign or_2_out = A | B;  // OR_Gate or_2, 16 bits wide
  assign xor_1_out = A ^ B;  // XOR_Gate xor_1, 16 bits wide
  assign not_2_out = ~or_2_out;  // NOT_Gate not_2, 16 bits wide
  Shift_Left_Logical shift_left_logical_1 (
    .Input(A), .CLK(clock_1_out), .SLL(in_6), .Output(shift_left_logical_1_output));
  Shift_Right_Logical shift_right_logical_1 (
    .in_1(A), .CLK(clock_2_out), .SRL(in_7), .Output(shift_right_logical_1_output));
  BEQ beq_1 (.A(A), .B(B), .BEQ(BEQ), .Output(beq_1_output));
  Register register_1 (
    .Data_IN(A), .RegWrite(in_9), .Data01(register_1_data01), .Data_Address(Address), .clk(CLK_out),
    .RS(in_11), .RT(in_12));  // open: Data02
  Adder #(.width(16)) adder_3 (.a(register_1_data01), .b(Immideate), .out(adder_3_out), .cin(in_8), .cout(out_17));
  assign or_3_out = register_1_data01 | Immideate;  // OR_Gate or_3, 16 bits wide
  assign and_2_out = register_1_data01 & Immideate;  // AND_Gate and_2, 16 bits wide
  Multiplexer #(.select(4), .width(16)) multiplexer_1 (
    .in0(adder_1_out), .in1(adder_3_out), .in2(adder_2_out), .in3(or_1_out), .in4(and_1_out),
    .in5(not_2_out), .in6(or_3_out), .in7(and_2_out), .in8(xor_1_out), .in9(shift_left_logical_1_output),
    .in10(shift_right_logical_1_output), .in11(beq_1_output), .out(Output), .sel(OP_Code));  // open: in12, in13, in14, in15, en

  // Notes on the sheet:
  //   FOR SHIFTING FIRST PARELLEL INPUT USNG CLOCK AND KEPPING SLL/SRL= 0, THEN MAKE SLL/SRL =1 AND USE CLOCK PULSE TO SHIFT
  //   16 Bit ALU
  //   ASIF MAHMUD
  //   WuW
  //   Niloy Biswash
  //   0000----ADD (A+B)
  //   0001---ADDi (A&IMMIDIATE)
  //   0010---SUB (A-B)
  //   0011---OR (A+B)
  //   0100---AND (A&B)
  //   0101---NOR ((A+B)')
  //   0110---ORi (A+IMMIDIATE)
  //   0111---ANDi (A & IMMIDIATE)
  //   1000---XOR (A'B+AB')
  //   1011---BEQ (BEQ=1  IF A==B)
  //   1100---JUMP(NOT IMPLEMENTED!)
  //   1101---MULT (NOT IMPLEMENTED!)
  //   1110--- LW (NOT IMPLEMENTED!)
  //   1111---SW(NOT IMPLEMENTED!)
  //   1001---SLL (SHIFT LEFT A USING CLOCK PULSE)
  //   1010---SRL (SHIFT RIGHT A USING CLOCK PULSE
endmodule

module Shift_Right_Logical (
  input  [15:0] in_1,
  input  CLK,
  input  SRL,
  output [15:0] Output
);

  wire multiplexer_1_out, multiplexer_2_out, multiplexer_3_out, multiplexer_4_out, multiplexer_5_out,
       multiplexer_6_out, multiplexer_7_out, multiplexer_8_out, multiplexer_9_out, multiplexer_10_out,
       multiplexer_11_out, multiplexer_12_out, multiplexer_13_out, multiplexer_14_out, multiplexer_15_out,
       multiplexer_16_out;

  D_Flip_Flop d_ff_1 (.clk(CLK), .D(multiplexer_1_out), .Q(Output[15]));  // open: Qn, preset, en, reset
  Multiplexer multiplexer_1 (.in0(in_1[15]), .in1(1'b0), .out(multiplexer_1_out), .sel(SRL));  // open: en
  D_Flip_Flop d_ff_2 (.clk(CLK), .D(multiplexer_2_out), .Q(Output[14]));  // open: Qn, preset, en, reset
  Multiplexer multiplexer_2 (.in0(in_1[14]), .in1(Output[15]), .out(multiplexer_2_out), .sel(SRL));  // open: en
  D_Flip_Flop d_ff_3 (.clk(CLK), .D(multiplexer_3_out), .Q(Output[13]));  // open: Qn, preset, en, reset
  Multiplexer multiplexer_3 (.in0(in_1[13]), .in1(Output[14]), .out(multiplexer_3_out), .sel(SRL));  // open: en
  Multiplexer multiplexer_4 (.in0(in_1[12]), .in1(Output[13]), .out(multiplexer_4_out), .sel(SRL));  // open: en
  D_Flip_Flop d_ff_4 (.clk(CLK), .D(multiplexer_4_out), .Q(Output[12]));  // open: Qn, preset, en, reset
  Multiplexer multiplexer_5 (.in0(in_1[11]), .in1(Output[12]), .out(multiplexer_5_out), .sel(SRL));  // open: en
  D_Flip_Flop d_ff_5 (.clk(CLK), .D(multiplexer_5_out), .Q(Output[11]));  // open: Qn, preset, en, reset
  Multiplexer multiplexer_6 (.in0(in_1[10]), .in1(Output[11]), .out(multiplexer_6_out), .sel(SRL));  // open: en
  D_Flip_Flop d_ff_6 (.clk(CLK), .D(multiplexer_6_out), .Q(Output[10]));  // open: Qn, preset, en, reset
  Multiplexer multiplexer_7 (.in0(in_1[9]), .in1(Output[10]), .out(multiplexer_7_out), .sel(SRL));  // open: en
  D_Flip_Flop d_ff_7 (.clk(CLK), .D(multiplexer_7_out), .Q(Output[9]));  // open: Qn, preset, en, reset
  Multiplexer multiplexer_8 (.in0(in_1[8]), .in1(Output[9]), .out(multiplexer_8_out), .sel(SRL));  // open: en
  D_Flip_Flop d_ff_8 (.clk(CLK), .D(multiplexer_8_out), .Q(Output[8]));  // open: Qn, preset, en, reset
  D_Flip_Flop d_ff_9 (.clk(CLK), .D(multiplexer_9_out), .Q(Output[7]));  // open: Qn, preset, en, reset
  Multiplexer multiplexer_9 (.in0(in_1[7]), .in1(Output[8]), .out(multiplexer_9_out), .sel(SRL));  // open: en
  D_Flip_Flop d_ff_10 (.clk(CLK), .D(multiplexer_10_out), .Q(Output[6]));  // open: Qn, preset, en, reset
  Multiplexer multiplexer_10 (.in0(in_1[6]), .in1(Output[7]), .out(multiplexer_10_out), .sel(SRL));  // open: en
  D_Flip_Flop d_ff_11 (.clk(CLK), .D(multiplexer_11_out), .Q(Output[5]));  // open: Qn, preset, en, reset
  Multiplexer multiplexer_11 (.in0(in_1[5]), .in1(Output[6]), .out(multiplexer_11_out), .sel(SRL));  // open: en
  Multiplexer multiplexer_12 (.in0(in_1[4]), .in1(Output[5]), .out(multiplexer_12_out), .sel(SRL));  // open: en
  D_Flip_Flop d_ff_12 (.clk(CLK), .D(multiplexer_12_out), .Q(Output[4]));  // open: Qn, preset, en, reset
  Multiplexer multiplexer_13 (.in0(in_1[3]), .in1(Output[4]), .out(multiplexer_13_out), .sel(SRL));  // open: en
  D_Flip_Flop d_ff_13 (.clk(CLK), .D(multiplexer_13_out), .Q(Output[3]));  // open: Qn, preset, en, reset
  Multiplexer multiplexer_14 (.in0(in_1[2]), .in1(Output[3]), .out(multiplexer_14_out), .sel(SRL));  // open: en
  D_Flip_Flop d_ff_14 (.clk(CLK), .D(multiplexer_14_out), .Q(Output[2]));  // open: Qn, preset, en, reset
  Multiplexer multiplexer_15 (.in0(in_1[1]), .in1(Output[2]), .out(multiplexer_15_out), .sel(SRL));  // open: en
  D_Flip_Flop d_ff_15 (.clk(CLK), .D(multiplexer_15_out), .Q(Output[1]));  // open: Qn, preset, en, reset
  Multiplexer multiplexer_16 (.in0(in_1[0]), .in1(Output[1]), .out(multiplexer_16_out), .sel(SRL));  // open: en
  D_Flip_Flop d_ff_16 (.clk(CLK), .D(multiplexer_16_out), .Q(Output[0]));  // open: Qn, preset, en, reset

  // Notes on the sheet:
  //   Asif Mahmud
  //   ID : 1511190642
endmodule

module Shift_Left_Logical (
  input  [15:0] Input,
  input  CLK,
  input  SLL,
  output [15:0] Output
);

  wire multiplexer_1_out, multiplexer_2_out, multiplexer_3_out, multiplexer_4_out, multiplexer_5_out,
       multiplexer_6_out, multiplexer_7_out, multiplexer_8_out, multiplexer_9_out, multiplexer_10_out,
       multiplexer_11_out, multiplexer_12_out, multiplexer_13_out, multiplexer_14_out, multiplexer_15_out,
       multiplexer_16_out;

  D_Flip_Flop d_ff_1 (.clk(CLK), .D(multiplexer_1_out), .Q(Output[15]));  // open: Qn, preset, en, reset
  Multiplexer multiplexer_1 (.in0(Input[15]), .in1(Output[14]), .out(multiplexer_1_out), .sel(SLL));  // open: en
  D_Flip_Flop d_ff_2 (.clk(CLK), .D(multiplexer_2_out), .Q(Output[14]));  // open: Qn, preset, en, reset
  Multiplexer multiplexer_2 (.in0(Input[14]), .in1(Output[13]), .out(multiplexer_2_out), .sel(SLL));  // open: en
  D_Flip_Flop d_ff_3 (.clk(CLK), .D(multiplexer_3_out), .Q(Output[13]));  // open: Qn, preset, en, reset
  Multiplexer multiplexer_3 (.in0(Input[13]), .in1(Output[12]), .out(multiplexer_3_out), .sel(SLL));  // open: en
  Multiplexer multiplexer_4 (.in0(Input[12]), .in1(Output[11]), .out(multiplexer_4_out), .sel(SLL));  // open: en
  D_Flip_Flop d_ff_4 (.clk(CLK), .D(multiplexer_4_out), .Q(Output[12]));  // open: Qn, preset, en, reset
  Multiplexer multiplexer_5 (.in0(Input[11]), .in1(Output[10]), .out(multiplexer_5_out), .sel(SLL));  // open: en
  D_Flip_Flop d_ff_5 (.clk(CLK), .D(multiplexer_5_out), .Q(Output[11]));  // open: Qn, preset, en, reset
  Multiplexer multiplexer_6 (.in0(Input[10]), .in1(Output[9]), .out(multiplexer_6_out), .sel(SLL));  // open: en
  D_Flip_Flop d_ff_6 (.clk(CLK), .D(multiplexer_6_out), .Q(Output[10]));  // open: Qn, preset, en, reset
  Multiplexer multiplexer_7 (.in0(Input[9]), .in1(Output[8]), .out(multiplexer_7_out), .sel(SLL));  // open: en
  D_Flip_Flop d_ff_7 (.clk(CLK), .D(multiplexer_7_out), .Q(Output[9]));  // open: Qn, preset, en, reset
  Multiplexer multiplexer_8 (.in0(Input[8]), .in1(Output[7]), .out(multiplexer_8_out), .sel(SLL));  // open: en
  D_Flip_Flop d_ff_8 (.clk(CLK), .D(multiplexer_8_out), .Q(Output[8]));  // open: Qn, preset, en, reset
  D_Flip_Flop d_ff_9 (.clk(CLK), .D(multiplexer_9_out), .Q(Output[7]));  // open: Qn, preset, en, reset
  Multiplexer multiplexer_9 (.in0(Input[7]), .in1(Output[6]), .out(multiplexer_9_out), .sel(SLL));  // open: en
  D_Flip_Flop d_ff_10 (.clk(CLK), .D(multiplexer_10_out), .Q(Output[6]));  // open: Qn, preset, en, reset
  Multiplexer multiplexer_10 (.in0(Input[6]), .in1(Output[5]), .out(multiplexer_10_out), .sel(SLL));  // open: en
  D_Flip_Flop d_ff_11 (.clk(CLK), .D(multiplexer_11_out), .Q(Output[5]));  // open: Qn, preset, en, reset
  Multiplexer multiplexer_11 (.in0(Input[5]), .in1(Output[4]), .out(multiplexer_11_out), .sel(SLL));  // open: en
  Multiplexer multiplexer_12 (.in0(Input[4]), .in1(Output[3]), .out(multiplexer_12_out), .sel(SLL));  // open: en
  D_Flip_Flop d_ff_12 (.clk(CLK), .D(multiplexer_12_out), .Q(Output[4]));  // open: Qn, preset, en, reset
  Multiplexer multiplexer_13 (.in0(Input[3]), .in1(Output[2]), .out(multiplexer_13_out), .sel(SLL));  // open: en
  D_Flip_Flop d_ff_13 (.clk(CLK), .D(multiplexer_13_out), .Q(Output[3]));  // open: Qn, preset, en, reset
  Multiplexer multiplexer_14 (.in0(Input[2]), .in1(Output[1]), .out(multiplexer_14_out), .sel(SLL));  // open: en
  D_Flip_Flop d_ff_14 (.clk(CLK), .D(multiplexer_14_out), .Q(Output[2]));  // open: Qn, preset, en, reset
  Multiplexer multiplexer_15 (.in0(Input[1]), .in1(Output[0]), .out(multiplexer_15_out), .sel(SLL));  // open: en
  D_Flip_Flop d_ff_15 (.clk(CLK), .D(multiplexer_15_out), .Q(Output[1]));  // open: Qn, preset, en, reset
  Multiplexer multiplexer_16 (.in0(Input[0]), .in1(1'b0), .out(multiplexer_16_out), .sel(SLL));  // open: en
  D_Flip_Flop d_ff_16 (.clk(CLK), .D(multiplexer_16_out), .Q(Output[0]));  // open: Qn, preset, en, reset

  // Notes on the sheet:
  //   Asif Mahmud
  //   ID-1511190642
  //   16 Bit Shift Left Logical
endmodule

module BEQ (
  input  [15:0] A,
  input  [15:0] B,
  output [15:0] Output,
  output BEQ
);

  wire [15:0] and_2_out, and_3_out, not_1_out, not_2_out;

  assign not_1_out = ~B;  // NOT_Gate not_1, 16 bits wide
  assign not_2_out = ~A;  // NOT_Gate not_2, 16 bits wide
  and and_1 (BEQ, Output[0], Output[1], Output[2], Output[3], Output[4], Output[5], Output[6], Output[7], Output[9], Output[10], Output[11], Output[12], Output[13], Output[14], Output[15]);
  assign and_2_out = not_2_out & not_1_out;  // AND_Gate and_2, 16 bits wide
  assign and_3_out = A & B;  // AND_Gate and_3, 16 bits wide
  assign Output = and_2_out | and_3_out;  // OR_Gate or_1, 16 bits wide

  // Notes on the sheet:
  //   16 Bit BEQ
  //   Asif Mahmud
  //   ID-1511190642
  //   If A & B is equal then BEQ is 1 else 0
  //   If A & B is equal Output is 1 else 0
endmodule

module Register (
  input  [15:0] Data_IN,
  input  RegWrite,
  input  [2:0] Data_Address,
  input  [2:0] RS,
  input  [2:0] RT,
  input  clk,
  output [15:0] Data01,
  output [15:0] Data02
);

  wire and_1_out, and_2_out, and_3_out, and_4_out, and_5_out, and_6_out, and_7_out, and_8_out,
       decoder_1_out0, decoder_1_out1, decoder_1_out2, decoder_1_out3, decoder_1_out4, decoder_1_out5,
       decoder_1_out6, decoder_1_out7;
  wire [15:0] register_1_q, register_2_q, register_3_q, register_4_q, register_5_q, register_6_q,
       register_7_q, Zero_q;

  Decoder #(.select(3)) decoder_1 (
    .out0(decoder_1_out0), .out1(decoder_1_out1), .out2(decoder_1_out2), .out3(decoder_1_out3),
    .out4(decoder_1_out4), .out5(decoder_1_out5), .out6(decoder_1_out6), .out7(decoder_1_out7),
    .sel(Data_Address));  // open: en
  and and_1 (and_1_out, decoder_1_out0, RegWrite);
  and and_2 (and_2_out, decoder_1_out1, RegWrite);
  and and_3 (and_3_out, decoder_1_out2, RegWrite);
  and and_4 (and_4_out, decoder_1_out3, RegWrite);
  and and_5 (and_5_out, decoder_1_out4, RegWrite);
  and and_6 (and_6_out, decoder_1_out5, RegWrite);
  and and_7 (and_7_out, decoder_1_out6, RegWrite);
  and and_8 (and_8_out, decoder_1_out7, RegWrite);
  Register_part #(.width(16)) Zero (.D(Data_IN), .en(and_1_out), .Q(Zero_q), .clk(clk));  // open: clr
  Register_part #(.width(16)) register_1 (.D(Data_IN), .en(and_2_out), .Q(register_1_q), .clk(clk));  // open: clr
  Register_part #(.width(16)) register_2 (.D(Data_IN), .en(and_3_out), .Q(register_2_q), .clk(clk));  // open: clr
  Register_part #(.width(16)) register_3 (.D(Data_IN), .en(and_4_out), .Q(register_3_q), .clk(clk));  // open: clr
  Register_part #(.width(16)) register_4 (.D(Data_IN), .en(and_5_out), .Q(register_4_q), .clk(clk));  // open: clr
  Register_part #(.width(16)) register_5 (.D(Data_IN), .en(and_6_out), .Q(register_5_q), .clk(clk));  // open: clr
  Register_part #(.width(16)) register_6 (.D(Data_IN), .en(and_7_out), .Q(register_6_q), .clk(clk));  // open: clr
  Register_part #(.width(16)) register_7 (.D(Data_IN), .en(and_8_out), .Q(register_7_q), .clk(clk));  // open: clr
  Multiplexer #(.select(3), .width(16)) multiplexer_1 (
    .in0(Zero_q), .in1(register_1_q), .in2(register_2_q), .in3(register_3_q), .in4(register_4_q),
    .in5(register_5_q), .in6(register_6_q), .in7(register_7_q), .out(Data01), .sel(RS));  // open: en
  Multiplexer #(.select(3), .width(16)) multiplexer_2 (
    .in0(Zero_q), .in1(register_1_q), .in2(register_2_q), .in3(register_3_q), .in4(register_4_q),
    .in5(register_5_q), .in6(register_6_q), .in7(register_7_q), .out(Data02), .sel(RT));  // open: en

  // Notes on the sheet:
  //   Register file
  //   Asif Mahmud
  //   ID : 1511190642
endmodule

module Andi (
  input  [15:0] in_1,
  input  in_2,
  input  [2:0] in_3,
  input  in_4,
  input  [2:0] in_5,
  input  [2:0] in_6,
  input  [15:0] Immidiate,
  output [15:0] out_8,
  output [15:0] out_9,
  output [15:0] out_10
);

  Register register_1 (
    .Data_IN(in_1), .RegWrite(in_2), .Data01(out_9), .Data02(out_10), .Data_Address(in_3), .clk(in_4),
    .RS(in_5), .RT(in_6));
  assign out_8 = out_9 & Immidiate;  // AND_Gate and_1, 16 bits wide

  // Notes on the sheet:
  //   Asif Mahmud
  //   ID : 1511190642
  //   And Immidiate using the Register file I built
endmodule

module ORi (
  input  [15:0] in_1,
  input  in_2,
  input  [2:0] in_3,
  input  in_4,
  input  [2:0] in_5,
  input  [2:0] in_6,
  input  [15:0] Immidiate,
  output [15:0] out_8,
  output [15:0] out_9,
  output [15:0] out_10
);

  Register register_1 (
    .Data_IN(in_1), .RegWrite(in_2), .Data01(out_9), .Data02(out_10), .Data_Address(in_3), .clk(in_4),
    .RS(in_5), .RT(in_6));
  assign out_8 = out_9 | Immidiate;  // OR_Gate or_1, 16 bits wide

  // Notes on the sheet:
  //   Asif Mahmud
  //   ID : 1511190642
  //   OR Immidiate using the Register file I built
endmodule

module ADDi (
  input  in_1,
  input  [15:0] in_2,
  input  in_3,
  input  [2:0] in_4,
  input  in_5,
  input  [2:0] in_6,
  input  [2:0] in_7,
  input  [15:0] Immidiate,
  output [15:0] out_9,
  output [15:0] out_10,
  output out_11,
  output [15:0] out_12
);

  Register register_1 (
    .Data_IN(in_2), .RegWrite(in_3), .Data01(out_10), .Data02(out_12), .Data_Address(in_4), .clk(in_5),
    .RS(in_6), .RT(in_7));
  Adder #(.width(16)) adder_1 (.a(out_10), .b(Immidiate), .out(out_9), .cin(in_1), .cout(out_11));

  // Notes on the sheet:
  //   Asif Mahmud
  //   ID : 1511190642
  //   ADD Immidiate using the Register file I built
endmodule

module CLA (
  input  C0,
  input  A0,
  input  A1,
  input  A2,
  input  A3,
  input  B0,
  input  B1,
  input  B2,
  input  B3,
  output C1,
  output C2,
  output C3,
  output C4
);

  wire and_1_out, C0P0P1_out, C0P0P1P2_out, C0P0P1P2P3_out, G0_out, G0P1_out, G0P1P2_out, G0P1P2P3_out,
       G1_out, G1P2_out, G1P2P3_out, G2_out, G2P3_out, G3_out, p0_out, p1_out, P2_out, P3_out;

  and G0 (G0_out, A0, B0);
  or p0 (p0_out, A0, B0);
  and G1 (G1_out, B1, A1);
  or p1 (p1_out, A1, B1);
  or P2 (P2_out, A2, B2);
  and G3 (G3_out, A3, B3);
  or P3 (P3_out, A3, B3);
  and G0P1 (G0P1_out, G0_out, p1_out);
  and G2 (G2_out, A2, B2);
  and G1P2 (G1P2_out, G1_out, P2_out);
  and G0P1P2 (G0P1P2_out, G0_out, p1_out, P2_out);
  and C0P0P1P2 (C0P0P1P2_out, C0, p0_out, p1_out, P2_out);
  and C0P0P1 (C0P0P1_out, C0, p0_out, p1_out);
  or or_1 (C3, G2_out, G1P2_out, G0P1P2_out, C0P0P1P2_out);
  and G2P3 (G2P3_out, G2_out, P3_out);
  and G1P2P3 (G1P2P3_out, G1_out, P2_out, P3_out);
  and and_1 (and_1_out, C0, p0_out);
  or or_2 (C2, G1_out, G0P1_out, C0P0P1_out);
  and G0P1P2P3 (G0P1P2P3_out, G0_out, p1_out, P2_out, P3_out);
  and C0P0P1P2P3 (C0P0P1P2P3_out, C0, p0_out, p1_out, P2_out, P3_out);
  or or_3 (C1, G0_out, and_1_out);
  or or_4 (C4, G3_out, G2P3_out, G1P2P3_out, G0P1P2P3_out, C0P0P1P2P3_out);

  // Notes on the sheet:
  //   ASIF MAHMUD
  //   ID-1511190642
  //   4 BIT CARRY LOOK AHEAD
endmodule

module Full_Adder (
  input  a,
  input  B,
  input  [15:0] in_3,
  input  C0,
  input  a_2,
  input  B_2,
  input  [15:0] A_3,
  input  a_4,
  input  B_3,
  input  [15:0] B_4,
  input  a_5,
  input  B_5,
  input  a_6,
  input  B_6,
  input  a_7,
  input  B_7,
  input  a_8,
  input  B_8,
  input  a_9,
  input  B_9,
  input  a_10,
  input  B_10,
  input  a_11,
  input  B_11,
  input  a_12,
  input  B_12,
  input  a_13,
  input  B_13,
  input  a_14,
  input  B_14,
  input  a_15,
  input  B_15,
  input  a_16,
  input  B_16,
  input  a_17,
  input  B_17,
  output SUM,
  output Cout,
  output SUM_2,
  output Cout_2,
  output SUM_3,
  output Cout_3,
  output SUM_4,
  output Cout_4,
  output SUM_5,
  output Cout_5,
  output SUM_6,
  output Cout_6,
  output SUM_7,
  output Cout_7,
  output SUM_8,
  output Cout_8,
  output SUM_9,
  output Cout_9,
  output SUM_10,
  output Cout_10,
  output SUM_11,
  output Cout_11,
  output SUM_12,
  output Cout_12,
  output SUM_13,
  output Cout_13,
  output SUM_14,
  output Cout_14,
  output SUM_15,
  output Cout_15,
  output SUM_16,
  output Cout_16,
  output Cout_17
);

  wire and_1_out, and_2_out, and_3_out, and_4_out, and_5_out, and_6_out, and_7_out, and_8_out, and_9_out,
       and_10_out, and_11_out, and_12_out, and_13_out, and_14_out, and_15_out, and_16_out, and_17_out,
       and_18_out, and_19_out, and_20_out, and_21_out, and_22_out, and_23_out, and_24_out, and_25_out,
       and_26_out, and_27_out, and_28_out, and_29_out, and_30_out, and_31_out, and_32_out, cla_1_c1,
       cla_1_c2, cla_1_c3, cla_2_c1, cla_2_c2, cla_2_c3, cla_2_c4, cla_3_c1, cla_3_c2, cla_3_c3, cla_3_c4,
       cla_4_c1, cla_4_c2, cla_4_c3, cla_4_c4, xor_1_out, xor_2_out, xor_3_out, xor_4_out, xor_5_out,
       xor_6_out, xor_7_out, xor_8_out, xor_9_out, xor_10_out, xor_11_out, xor_12_out, xor_13_out,
       xor_14_out, xor_15_out, xor_16_out;

  CLA cla_1 (
    .C0(cla_2_c4), .A0(A_3[12]), .A1(A_3[13]), .A2(A_3[14]), .A3(A_3[15]), .B0(B_4[12]), .B1(B_4[13]),
    .B2(B_4[14]), .B3(B_4[15]), .C1(cla_1_c1), .C2(cla_1_c2), .C3(cla_1_c3), .C4(Cout_16));
  CLA cla_2 (
    .C0(cla_4_c4), .A0(A_3[8]), .A1(A_3[9]), .A2(A_3[10]), .A3(A_3[11]), .B0(B_4[8]), .B1(B_4[9]),
    .B2(B_4[10]), .B3(B_4[11]), .C1(cla_2_c1), .C2(cla_2_c2), .C3(cla_2_c3), .C4(cla_2_c4));
  CLA cla_3 (
    .C0(C0), .A0(a), .A1(a_2), .A2(A_3[2]), .A3(A_3[3]), .B0(B), .B1(B_2), .B2(B_4[2]), .B3(B_4[3]),
    .C1(cla_3_c1), .C2(cla_3_c2), .C3(cla_3_c3), .C4(cla_3_c4));
  CLA cla_4 (
    .C0(cla_3_c4), .A0(A_3[4]), .A1(A_3[5]), .A2(A_3[6]), .A3(A_3[7]), .B0(B_4[4]), .B1(B_4[5]), .B2(B_4[6]),
    .B3(B_4[7]), .C1(cla_4_c1), .C2(cla_4_c2), .C3(cla_4_c3), .C4(cla_4_c4));
  xor xor_1 (xor_1_out, a, B);
  xor xor_2 (xor_2_out, a_2, B_2);
  xor xor_3 (xor_3_out, A_3[2], B_3);
  xor xor_4 (xor_4_out, A_3[3], B_4[2]);
  xor xor_5 (xor_5_out, A_3[4], B_4[3]);
  xor xor_6 (xor_6_out, A_3[5], B_4[4]);
  xor xor_7 (xor_7_out, A_3[6], B_4[5]);
  xor xor_8 (xor_8_out, A_3[7], B_4[6]);
  xor xor_9 (xor_9_out, a_10, B_4[7]);
  xor xor_10 (xor_10_out, A_3[8], B_4[8]);
  xor xor_11 (xor_11_out, A_3[9], B_4[9]);
  xor xor_12 (xor_12_out, A_3[10], B_4[10]);
  xor xor_13 (xor_13_out, A_3[11], B_4[11]);
  xor xor_14 (xor_14_out, A_3[12], B_4[12]);
  xor xor_15 (xor_15_out, A_3[13], B_4[13]);
  xor xor_16 (xor_16_out, A_3[14], B_4[14]);
  xor xor_17 (in_3[0], xor_1_out, C0);
  and and_1 (and_1_out, xor_1_out, C0);
  and and_2 (and_2_out, a, B);
  xor xor_18 (in_3[1], xor_2_out, cla_3_c1);
  and and_3 (and_3_out, xor_2_out, cla_3_c1);
  and and_4 (and_4_out, a_2, B_2);
  xor xor_19 (in_3[2], xor_3_out, cla_3_c2);
  and and_5 (and_5_out, xor_3_out, cla_3_c2);
  and and_6 (and_6_out, A_3[2], B_3);
  xor xor_20 (in_3[3], xor_4_out, cla_3_c3);
  and and_7 (and_7_out, xor_4_out, cla_3_c3);
  and and_8 (and_8_out, A_3[3], B_4[2]);
  xor xor_21 (in_3[4], xor_5_out, cla_3_c4);
  and and_9 (and_9_out, xor_5_out, cla_3_c4);
  and and_10 (and_10_out, A_3[4], B_4[3]);
  xor xor_22 (in_3[5], xor_6_out, cla_4_c1);
  and and_11 (and_11_out, xor_6_out, cla_4_c1);
  and and_12 (and_12_out, A_3[5], B_4[4]);
  xor xor_23 (in_3[6], xor_7_out, cla_4_c2);
  and and_13 (and_13_out, xor_7_out, cla_4_c2);
  and and_14 (and_14_out, A_3[6], B_4[5]);
  xor xor_24 (in_3[7], xor_8_out, cla_4_c3);
  and and_15 (and_15_out, xor_8_out, cla_4_c3);
  and and_16 (and_16_out, A_3[7], B_4[6]);
  xor xor_25 (in_3[8], xor_9_out, cla_4_c4);
  and and_17 (and_17_out, xor_9_out, cla_4_c4);
  and and_18 (and_18_out, a_10, B_4[7]);
  xor xor_26 (in_3[9], xor_10_out, cla_2_c1);
  and and_19 (and_19_out, xor_10_out, cla_2_c1);
  and and_20 (and_20_out, A_3[8], B_4[8]);
  xor xor_27 (in_3[10], xor_11_out, cla_2_c2);
  and and_21 (and_21_out, xor_11_out, cla_2_c2);
  and and_22 (and_22_out, A_3[9], B_4[9]);
  xor xor_28 (in_3[11], xor_12_out, cla_2_c3);
  and and_23 (and_23_out, xor_12_out, cla_2_c3);
  and and_24 (and_24_out, A_3[10], B_4[10]);
  xor xor_29 (in_3[12], xor_13_out, cla_2_c4);
  and and_25 (and_25_out, xor_13_out, cla_2_c4);
  and and_26 (and_26_out, A_3[11], B_4[11]);
  xor xor_30 (in_3[13], xor_14_out, cla_1_c1);
  and and_27 (and_27_out, xor_14_out, cla_1_c1);
  and and_28 (and_28_out, A_3[12], B_4[12]);
  xor xor_31 (in_3[14], xor_15_out, cla_1_c2);
  and and_29 (and_29_out, xor_15_out, cla_1_c2);
  and and_30 (and_30_out, A_3[13], B_4[13]);
  xor xor_32 (in_3[15], xor_16_out, cla_1_c3);
  and and_31 (and_31_out, xor_16_out, cla_1_c3);
  and and_32 (and_32_out, A_3[14], B_4[14]);
  or or_1 (Cout, and_1_out, and_2_out);
  or or_2 (Cout_2, and_3_out, and_4_out);
  or or_3 (Cout_3, and_5_out, and_6_out);
  or or_4 (Cout_4, and_7_out, and_8_out);
  or or_5 (Cout_5, and_9_out, and_10_out);
  or or_6 (Cout_6, and_11_out, and_12_out);
  or or_7 (Cout_7, and_13_out, and_14_out);
  or or_8 (Cout_8, and_15_out, and_16_out);
  or or_9 (Cout_9, and_17_out, and_18_out);
  or or_10 (Cout_10, and_19_out, and_20_out);
  or or_11 (Cout_11, and_21_out, and_22_out);
  or or_12 (Cout_12, and_23_out, and_24_out);
  or or_13 (Cout_13, and_25_out, and_26_out);
  or or_14 (Cout_14, and_27_out, and_28_out);
  or or_15 (Cout_15, and_29_out, and_30_out);
  or or_16 (Cout_17, and_31_out, and_32_out);

  assign A_3[1:0] = {a_2, a};
  assign a_4 = A_3[2];
  assign a_5 = A_3[3];
  assign a_6 = A_3[4];
  assign a_7 = A_3[5];
  assign a_8 = A_3[6];
  assign a_9 = A_3[7];
  assign a_11 = A_3[8];
  assign a_12 = A_3[9];
  assign a_13 = A_3[10];
  assign a_14 = A_3[11];
  assign a_15 = A_3[12];
  assign a_16 = A_3[13];
  assign a_17 = A_3[14];
  assign B_4[1:0] = {B_2, B};
  assign B_5 = B_4[2];
  assign B_6 = B_4[3];
  assign B_7 = B_4[4];
  assign B_8 = B_4[5];
  assign B_9 = B_4[6];
  assign B_10 = B_4[7];
  assign B_11 = B_4[8];
  assign B_12 = B_4[9];
  assign B_13 = B_4[10];
  assign B_14 = B_4[11];
  assign B_15 = B_4[12];
  assign B_16 = B_4[13];
  assign B_17 = B_4[14];
  assign SUM = in_3[0];
  assign SUM_2 = in_3[1];
  assign SUM_3 = in_3[2];
  assign SUM_4 = in_3[3];
  assign SUM_5 = in_3[4];
  assign SUM_6 = in_3[5];
  assign SUM_7 = in_3[6];
  assign SUM_8 = in_3[7];
  assign SUM_9 = in_3[8];
  assign SUM_10 = in_3[9];
  assign SUM_11 = in_3[10];
  assign SUM_12 = in_3[11];
  assign SUM_13 = in_3[12];
  assign SUM_14 = in_3[13];
  assign SUM_15 = in_3[14];
  assign SUM_16 = in_3[15];

  // Notes on the sheet:
  //   ASIF MAHMUD
  //   ID-1511190642
  //   THERE IS SOME ERROR COULDN'T FINISH
endmodule

module _1_bit_adder (
  input  in_1,
  input  in_2,
  input  cin,
  output s,
  output cout
);

  wire and_1_out, and_2_out, and_3_out, xor_1_out;

  xor xor_1 (xor_1_out, in_1, in_2);
  and and_1 (and_1_out, cin, in_1);
  and and_2 (and_2_out, cin, in_2);
  and and_3 (and_3_out, in_2, in_1);
  xor xor_2 (s, xor_1_out, cin);
  or or_1 (cout, and_1_out, and_2_out, and_3_out);
endmodule

module _16_Bit_CLA (
  input  Cin,
  input  [15:0] in_2,
  input  [15:0] in_3,
  output [15:0] Out_put,
  output Cout
);

  wire cla_1_c1, cla_1_c2, cla_1_c3, cla_1_c4, cla_2_c1, cla_2_c2, cla_2_c3, cla_2_c4, cla_3_c1, cla_3_c2,
       cla_3_c3, cla_3_c4, cla_4_c1, cla_4_c2, cla_4_c3;

  CLA cla_1 (
    .C0(Cin), .A0(in_2[0]), .A1(in_2[1]), .A2(in_2[2]), .A3(in_2[3]), .B0(in_3[0]), .B1(in_3[1]),
    .B2(in_3[2]), .B3(in_3[3]), .C1(cla_1_c1), .C2(cla_1_c2), .C3(cla_1_c3), .C4(cla_1_c4));
  CLA cla_2 (
    .C0(cla_1_c4), .A0(in_2[4]), .A1(in_2[5]), .A2(in_2[6]), .A3(in_2[7]), .B0(in_3[4]), .B1(in_3[5]),
    .B2(in_3[6]), .B3(in_3[7]), .C1(cla_2_c1), .C2(cla_2_c2), .C3(cla_2_c3), .C4(cla_2_c4));
  CLA cla_3 (
    .C0(cla_2_c4), .A0(in_2[8]), .A1(in_2[9]), .A2(in_2[10]), .A3(in_2[11]), .B0(in_3[8]), .B1(in_3[9]),
    .B2(in_3[10]), .B3(in_3[11]), .C1(cla_3_c1), .C2(cla_3_c2), .C3(cla_3_c3), .C4(cla_3_c4));
  CLA cla_4 (
    .C0(cla_3_c4), .A0(in_2[12]), .A1(in_2[13]), .A2(in_2[14]), .A3(in_2[15]), .B0(in_3[12]), .B1(in_3[13]),
    .B2(in_3[14]), .B3(in_3[15]), .C1(cla_4_c1), .C2(cla_4_c2), .C3(cla_4_c3), .C4(Cout));
  _1_bit_adder u_1_bit_adder_1 (.in_1(in_2[0]), .in_2(in_3[0]), .cin(Cin), .s(Out_put[0]));  // open: cout
  _1_bit_adder u_1_bit_adder_2 (.in_1(in_2[1]), .in_2(in_3[1]), .cin(cla_1_c1), .s(Out_put[1]));  // open: cout
  _1_bit_adder u_1_bit_adder_3 (.in_1(in_2[2]), .in_2(in_3[2]), .cin(cla_1_c2), .s(Out_put[2]));  // open: cout
  _1_bit_adder u_1_bit_adder_4 (.in_1(in_2[3]), .in_2(in_3[3]), .cin(cla_1_c3), .s(Out_put[3]));  // open: cout
  _1_bit_adder u_1_bit_adder_5 (.in_1(in_2[4]), .in_2(in_3[4]), .cin(cla_1_c4), .s(Out_put[4]));  // open: cout
  _1_bit_adder u_1_bit_adder_6 (.in_1(in_2[5]), .in_2(in_3[5]), .cin(cla_2_c1), .s(Out_put[5]));  // open: cout
  _1_bit_adder u_1_bit_adder_7 (.in_1(in_2[6]), .in_2(in_3[6]), .cin(cla_2_c2), .s(Out_put[6]));  // open: cout
  _1_bit_adder u_1_bit_adder_8 (.in_1(in_2[7]), .in_2(in_3[7]), .cin(cla_2_c3), .s(Out_put[7]));  // open: cout
  _1_bit_adder u_1_bit_adder_9 (.in_1(in_2[8]), .in_2(in_3[8]), .cin(cla_2_c4), .s(Out_put[8]));  // open: cout
  _1_bit_adder u_1_bit_adder_10 (.in_1(in_2[9]), .in_2(in_3[9]), .cin(cla_3_c1), .s(Out_put[9]));  // open: cout
  _1_bit_adder u_1_bit_adder_11 (.in_1(in_2[10]), .in_2(in_3[10]), .cin(cla_3_c2), .s(Out_put[10]));  // open: cout
  _1_bit_adder u_1_bit_adder_12 (.in_1(in_2[11]), .in_2(in_3[11]), .cin(cla_3_c3), .s(Out_put[11]));  // open: cout
  _1_bit_adder u_1_bit_adder_13 (.in_1(in_2[12]), .in_2(in_3[12]), .cin(cla_3_c4), .s(Out_put[12]));  // open: cout
  _1_bit_adder u_1_bit_adder_14 (.in_1(in_2[13]), .in_2(in_3[13]), .cin(cla_4_c1), .s(Out_put[13]));  // open: cout
  _1_bit_adder u_1_bit_adder_15 (.in_1(in_2[14]), .in_2(in_3[14]), .cin(cla_4_c2), .s(Out_put[14]));  // open: cout
  _1_bit_adder u_1_bit_adder_16 (.in_1(in_2[15]), .in_2(in_3[15]), .cin(cla_4_c3), .s(Out_put[15]));  // open: cout

  // Notes on the sheet:
  //   B
  //   16 Bit CLA
  //   ASIF MAHMUD
  //   A
  //   1
  //   2
  //   3
  //   4
  //   5
  //   6
  //   7
  //   8
  //   9
  //   10
  //   11
  //   12
  //   13
  //   14
  //   15
  //   16
endmodule
