// Logisim project ADDi.circ as structural Verilog: 2 circuits, main circuit main
module main (
  input  [15:0] in_1,
  input  in_2,
  input  [2:0] in_3,
  input  [2:0] in_4,
  input  [2:0] in_5,
  input  [15:0] Immidiate,
  output [15:0] out_7,
  output [15:0] out_8,
  output [15:0] out_9
);

  wire CLK_out;

  Clock CLK (.out(CLK_out));
  Register register_1 (
    .Data_IN(in_1), .RegWrite(in_2), .Data01(out_7), .Data02(out_9), .Data_Address(in_3), .clk(CLK_out),
    .RS(in_4), .RT(in_5));
  Adder #(.width(16)) adder_1 (.a(out_7), .b(Immidiate), .out(out_8));  // open: cin, cout

  // Notes on the sheet:
  //   ASIF MAHMUD
  //   ID-1511190642
  //   USING THE REGISTER FILE I BUILT
endmodule

module Register (
  input  [15:0] Data_IN,
  input  RegWrite,
  input  [2:0] Data_Address,
  input  [2:0] RS,
  input  [2:0] RT,
  input  clk,
  output [15:0] Data01,
  output [15:0] Data02
);

  wire and_1_out, and_2_out, and_3_out, and_4_out, and_5_out, and_6_out, and_7_out, and_8_out,
       decoder_1_out0, decoder_1_out1, decoder_1_out2, decoder_1_out3, decoder_1_out4, decoder_1_out5,
       decoder_1_out6, decoder_1_out7;
  wire [15:0] register_1_q, register_2_q, register_3_q, register_4_q, register_5_q, register_6_q,
       register_7_q, Zero_q;

  Decoder #(.select(3)) decoder_1 (
    .out0(decoder_1_out0), .out1(decoder_1_out1), .out2(decoder_1_out2), .out3(decoder_1_out3),
    .out4(decoder_1_out4), .out5(decoder_1_out5), .out6(decoder_1_out6), .out7(decoder_1_out7),
    .sel(Data_Address));  // open: en
  and and_1 (and_1_out, decoder_1_out0, RegWrite);
  and and_2 (and_2_out, decoder_1_out1, RegWrite);
  and and_3 (and_3_out, decoder_1_out2, RegWrite);
  and and_4 (and_4_out, decoder_1_out3, RegWrite);
  and and_5 (and_5_out, decoder_1_out4, RegWrite);
  and and_6 (and_6_out, decoder_1_out5, RegWrite);
  and and_7 (and_7_out, decoder_1_out6, RegWrite);
  and and_8 (and_8_out, decoder_1_out7, RegWrite);
  Register_part #(.width(16)) Zero (.D(Data_IN), .en(and_1_out), .Q(Zero_q), .clk(clk));  // open: clr
  Register_part #(.width(16)) register_1 (.D(Data_IN), .en(and_2_out), .Q(register_1_q), .clk(clk));  // open: clr
  Register_part #(.width(16)) register_2 (.D(Data_IN), .en(and_3_out), .Q(register_2_q), .clk(clk));  // open: clr
  Register_part #(.width(16)) register_3 (.D(Data_IN), .en(and_4_out), .Q(register_3_q), .clk(clk));  // open: clr
  Register_part #(.width(16)) register_4 (.D(Data_IN), .en(and_5_out), .Q(register_4_q), .clk(clk));  // open: clr
  Register_part #(.width(16)) register_5 (.D(Data_IN), .en(and_6_out), .Q(register_5_q), .clk(clk));  // open: clr
  Register_part #(.width(16)) register_6 (.D(Data_IN), .en(and_7_out), .Q(register_6_q), .clk(clk));  // open: clr
  Register_part #(.width(16)) register_7 (.D(Data_IN), .en(and_8_out), .Q(register_7_q), .clk(clk));  // open: clr
  Multiplexer #(.select(3), .width(16)) multiplexer_1 (
    .in0(Zero_q), .in1(register_1_q), .in2(register_2_q), .in3(register_3_q), .in4(register_4_q),
    .in5(register_5_q), .in6(register_6_q), .in7(register_7_q), .out(Data01), .sel(RS));  // open: en
  Multiplexer #(.select(3), .width(16)) multiplexer_2 (
    .in0(Zero_q), .in1(register_1_q), .in2(register_2_q), .in3(register_3_q), .in4(register_4_q),
    .in5(register_5_q), .in6(register_6_q), .in7(register_7_q), .out(Data02), .sel(RT));  // open: en

  // Notes on the sheet:
  //   Register file
  //   Asif Mahmud
  //   ID : 1511190642
endmodule
