// Logisim project BEQ.circ as structural Verilog: 1 circuit, main circuit main
module main (
  input  [15:0] A,
  input  [15:0] B,
  output [15:0] Output,
  output BEQ
);

  wire [15:0] and_2_out, and_3_out, not_1_out, not_2_out;

  assign not_1_out = ~B;  // NOT_Gate not_1, 16 bits wide
  assign not_2_out = ~A;  // NOT_Gate not_2, 16 bits wide
  and and_1 (BEQ, Output[0], Output[1], Output[2], Output[3], Output[4], Output[5], Output[6], Output[7], Output[9], Output[10], Output[11], Output[12], Output[13], Output[14], Output[15]);
  assign and_2_out = not_2_out & not_1_out;  // AND_Gate and_2, 16 bits wide
  assign and_3_out = A & B;  // AND_Gate and_3, 16 bits wide
  assign Output = and_2_out | and_3_out;  // OR_Gate or_1, 16 bits wide

  // Notes on the sheet:
  //   16 Bit BEQ
  //   Asif Mahmud
  //   ID-1511190642
  //   If A & B is equal then BEQ is 1 else 0
  //   If A & B is equal Output is 1 else 0
endmodule
