// Logisim project Carry Lookahead Adder.circ as structural Verilog: 1 circuit, main circuit main
module main (
  input  C0,
  input  A0,
  input  A1,
  input  A2,
  input  A3,
  input  B0,
  input  B1,
  input  B2,
  input  B3,
  output C1,
  output C2,
  output C3,
  output C4
);

  wire and_1_out, C0P0P1_out, C0P0P1P2_out, C0P0P1P2P3_out, G0_out, G0P1_out, G0P1P2_out, G0P1P2P3_out,
       G1_out, G1P2_out, G1P2P3_out, G2_out, G2P3_out, G3_out, p0_out, p1_out, P2_out, P3_out;

  and G0 (G0_out, A0, B0);
  or p0 (p0_out, A0, B0);
  and G1 (G1_out, B1, A1);
  or p1 (p1_out, A1, B1);
  or P2 (P2_out, A2, B2);
  and G3 (G3_out, A3, B3);
  or P3 (P3_out, A3, B3);
  or G0P1 (G0P1_out, G0_out, p1_out);
  and G2 (G2_out, A2, B2);
  and G1P2 (G1P2_out, G1_out, P2_out);
  and G0P1P2 (G0P1P2_out, G0_out, p1_out, P2_out);
  and C0P0P1P2 (C0P0P1P2_out, C0, p0_out, p1_out, P2_out);
  and C0P0P1 (C0P0P1_out, C0, p0_out, p1_out);
  or or_1 (C3, G2_out, G1P2_out, G0P1P2_out, C0P0P1P2_out);
  and G2P3 (G2P3_out, G2_out, P3_out);
  and G1P2P3 (G1P2P3_out, G1_out, P2_out, P3_out);
  and and_1 (and_1_out, C0, p0_out);
  or or_2 (C2, G1_out, G0P1_out, C0P0P1_out);
  and G0P1P2P3 (G0P1P2P3_out, G0_out, p1_out, P2_out, P3_out);
  and C0P0P1P2P3 (C0P0P1P2P3_out, C0, p0_out, p1_out, P2_out, P3_out);
  or or_3 (C1, G0_out, and_1_out);
  or or_4 (C4, G3_out, G2P3_out, G1P2P3_out, G0P1P2P3_out, C0P0P1P2P3_out);

  // Notes on the sheet:
  //   ASIF MAHMUD
  //   ID-1511190642
  //   4 BIT CARRY LOOK AHEAD
endmodule
