// Logisim project Shift Right Logical.circ as structural Verilog: 1 circuit, main circuit Shift Right Logical
module Shift_Right_Logical (
  input  [15:0] Input,
  input  SRL,
  output [15:0] Output
);

  wire clock_1_out, multiplexer_1_out, multiplexer_2_out, multiplexer_3_out, multiplexer_4_out,
       multiplexer_5_out, multiplexer_6_out, multiplexer_7_out, multiplexer_8_out, multiplexer_9_out,
       multiplexer_10_out, multiplexer_11_out, multiplexer_12_out, multiplexer_13_out, multiplexer_14_out,
       multiplexer_15_out, multiplexer_16_out;

  Clock clock_1 (.out(clock_1_out));
  D_Flip_Flop d_ff_1 (.clk(clock_1_out), .D(multiplexer_1_out), .Q(Output[15]));  // open: Qn, preset, en, reset
  Multiplexer multiplexer_1 (.in0(Input[15]), .in1(1'b0), .out(multiplexer_1_out), .sel(SRL));  // open: en
  D_Flip_Flop d_ff_2 (.clk(clock_1_out), .D(multiplexer_2_out), .Q(Output[14]));  // open: Qn, preset, en, reset
  Multiplexer multiplexer_2 (.in0(Input[14]), .in1(Output[15]), .out(multiplexer_2_out), .sel(SRL));  // open: en
  D_Flip_Flop d_ff_3 (.clk(clock_1_out), .D(multiplexer_3_out), .Q(Output[13]));  // open: Qn, preset, en, reset
  Multiplexer multiplexer_3 (.in0(Input[13]), .in1(Output[14]), .out(multiplexer_3_out), .sel(SRL));  // open: en
  Multiplexer multiplexer_4 (.in0(Input[12]), .in1(Output[13]), .out(multiplexer_4_out), .sel(SRL));  // open: en
  D_Flip_Flop d_ff_4 (.clk(clock_1_out), .D(multiplexer_4_out), .Q(Output[12]));  // open: Qn, preset, en, reset
  Multiplexer multiplexer_5 (.in0(Input[11]), .in1(Output[12]), .out(multiplexer_5_out), .sel(SRL));  // open: en
  D_Flip_Flop d_ff_5 (.clk(clock_1_out), .D(multiplexer_5_out), .Q(Output[11]));  // open: Qn, preset, en, reset
  Multiplexer multiplexer_6 (.in0(Input[10]), .in1(Output[11]), .out(multiplexer_6_out), .sel(SRL));  // open: en
  D_Flip_Flop d_ff_6 (.clk(clock_1_out), .D(multiplexer_6_out), .Q(Output[10]));  // open: Qn, preset, en, reset
  Multiplexer multiplexer_7 (.in0(Input[9]), .in1(Output[10]), .out(multiplexer_7_out), .sel(SRL));  // open: en
  D_Flip_Flop d_ff_7 (.clk(clock_1_out), .D(multiplexer_7_out), .Q(Output[9]));  // open: Qn, preset, en, reset
  Multiplexer multiplexer_8 (.in0(Input[8]), .in1(Output[9]), .out(multiplexer_8_out), .sel(SRL));  // open: en
  D_Flip_Flop d_ff_8 (.clk(clock_1_out), .D(multiplexer_9_out), .Q(Output[7]));  // open: Qn, preset, en, reset
  D_Flip_Flop d_ff_9 (.clk(clock_1_out), .D(multiplexer_8_out), .Q(Output[8]));  // open: Qn, preset, en, reset
  Multiplexer multiplexer_9 (.in0(Input[7]), .in1(Output[8]), .out(multiplexer_9_out), .sel(SRL));  // open: en
  D_Flip_Flop d_ff_10 (.clk(clock_1_out), .D(multiplexer_10_out), .Q(Output[6]));  // open: Qn, preset, en, reset
  Multiplexer multiplexer_10 (.in0(Input[6]), .in1(Output[7]), .out(multiplexer_10_out), .sel(SRL));  // open: en
  D_Flip_Flop d_ff_11 (.clk(clock_1_out), .D(multiplexer_12_out), .Q(Output[5]));  // open: Qn, preset, en, reset
  Multiplexer multiplexer_11 (.in0(Input[4]), .in1(Output[5]), .out(multiplexer_11_out), .sel(SRL));  // open: en
  Multiplexer multiplexer_12 (.in0(Input[5]), .in1(Output[6]), .out(multiplexer_12_out), .sel(SRL));  // open: en
  D_Flip_Flop d_ff_12 (.clk(clock_1_out), .D(multiplexer_11_out), .Q(Output[4]));  // open: Qn, preset, en, reset
  Multiplexer multiplexer_13 (.in0(Input[3]), .in1(Output[4]), .out(multiplexer_13_out), .sel(SRL));  // open: en
  D_Flip_Flop d_ff_13 (.clk(clock_1_out), .D(multiplexer_13_out), .Q(Output[3]));  // open: Qn, preset, en, reset
  Multiplexer multiplexer_14 (.in0(Input[2]), .in1(Output[3]), .out(multiplexer_14_out), .sel(SRL));  // open: en
  D_Flip_Flop d_ff_14 (.clk(clock_1_out), .D(multiplexer_14_out), .Q(Output[2]));  // open: Qn, preset, en, reset
  Multiplexer multiplexer_15 (.in0(Input[1]), .in1(Output[2]), .out(multiplexer_15_out), .sel(SRL));  // open: en
  D_Flip_Flop d_ff_15 (.clk(clock_1_out), .D(multiplexer_15_out), .Q(Output[1]));  // open: Qn, preset, en, reset
  Multiplexer multiplexer_16 (.in0(Input[0]), .in1(Output[1]), .out(multiplexer_16_out), .sel(SRL));  // open: en
  D_Flip_Flop d_ff_16 (.clk(clock_1_out), .D(multiplexer_16_out), .Q(Output[0]));  // open: Qn, preset, en, reset

  // Notes on the sheet:
  //   Asif Mahmud
  //   ID : 1511190642
  //   16 Bit Shift Right Logical
endmodule
