// Logisim project NonPipelineCpu2.circ as structural Verilog: 14 circuits, main circuit BEQ
module BEQ (
  input  [15:0] A,
  input  [15:0] B,
  output [15:0] Output,
  output BEQ
);

  nor nor_1 (BEQ, Output[0], Output[1], Output[2], Output[3], Output[4], Output[5], Output[6], Output[7], Output[8], Output[9], Output[10], Output[11], Output[12], Output[13], Output[14], Output[15]);
  Subtractor #(.width(16)) subtractor_1 (.a(A), .b(B), .out(Output));  // open: bin, bout

  // Notes on the sheet:
  //   BEQ / BNE
  //   Niloy Biswas
  //   ID- 1520022042
  //   If A & B is equal then BEQ is 1 else 0
endmodule

module CLA (
  input  C0,
  input  A0,
  input  A1,
  input  A2,
  input  A3,
  input  B0,
  input  B1,
  input  B2,
  input  B3,
  output C1,
  output C2,
  output C3,
  output C4
);

  wire and_1_out, C0P0P1_out, C0P0P1P2_out, C0P0P1P2P3_out, G0_out, G0P1_out, G0P1P2_out, G0P1P2P3_out,
       G1_out, G1P2_out, G1P2P3_out, G2_out, G2P3_out, G3_out, p0_out, p1_out, P2_out, P3_out;

  and G0 (G0_out, A0, B0);
  or p0 (p0_out, A0, B0);
  and G1 (G1_out, B1, A1);
  or p1 (p1_out, A1, B1);
  or P2 (P2_out, A2, B2);
  and G3 (G3_out, A3, B3);
  or P3 (P3_out, A3, B3);
  and G0P1 (G0P1_out, G0_out, p1_out);
  and G2 (G2_out, A2, B2);
  and G1P2 (G1P2_out, G1_out, P2_out);
  and G0P1P2 (G0P1P2_out, G0_out, p1_out, P2_out);
  and C0P0P1P2 (C0P0P1P2_out, C0, p0_out, p1_out, P2_out);
  and C0P0P1 (C0P0P1_out, C0, p0_out, p1_out);
  or or_1 (C3, G2_out, G1P2_out, G0P1P2_out, C0P0P1P2_out);
  and G2P3 (G2P3_out, G2_out, P3_out);
  and G1P2P3 (G1P2P3_out, G1_out, P2_out, P3_out);
  and and_1 (and_1_out, C0, p0_out);
  or or_2 (C2, G1_out, G0P1_out, C0P0P1_out);
  and G0P1P2P3 (G0P1P2P3_out, G0_out, p1_out, P2_out, P3_out);
  and C0P0P1P2P3 (C0P0P1P2P3_out, C0, p0_out, p1_out, P2_out, P3_out);
  or or_3 (C1, G0_out, and_1_out);
  or or_4 (C4, G3_out, G2P3_out, G1P2P3_out, G0P1P2P3_out, C0P0P1P2P3_out);

  // Notes on the sheet:
  //   4 BIT CARRY LOOK AHEAD
  //   ASIF MAHMUD
  //   ID-1511190642
endmodule

module _1_bit_adder (
  input  in_1,
  input  in_2,
  input  cin,
  output s,
  output cout
);

  wire and_1_out, and_2_out, and_3_out, xor_1_out;

  xor xor_1 (xor_1_out, in_1, in_2);
  and and_1 (and_1_out, cin, in_1);
  and and_2 (and_2_out, cin, in_2);
  and and_3 (and_3_out, in_2, in_1);
  xor xor_2 (s, xor_1_out, cin);
  or or_1 (cout, and_1_out, and_2_out, and_3_out);

  // Notes on the sheet:
  //   ASIF MAHMUD
  //   ID- 1511190642
endmodule

module _16_Bit_CLA (
  input  Cin,
  input  [15:0] in_2,
  input  [15:0] in_3,
  output [15:0] Out_put,
  output Cout
);

  wire cla_1_c1, cla_1_c2, cla_1_c3, cla_1_c4, cla_2_c1, cla_2_c2, cla_2_c3, cla_2_c4, cla_3_c1, cla_3_c2,
       cla_3_c3, cla_3_c4, cla_4_c1, cla_4_c2, cla_4_c3;

  CLA cla_1 (
    .C0(Cin), .A0(in_2[0]), .A1(in_2[1]), .A2(in_2[2]), .A3(in_2[3]), .B0(in_3[0]), .B1(in_3[1]),
    .B2(in_3[2]), .B3(in_3[3]), .C1(cla_1_c1), .C2(cla_1_c2), .C3(cla_1_c3), .C4(cla_1_c4));
  CLA cla_2 (
    .C0(cla_1_c4), .A0(in_2[4]), .A1(in_2[5]), .A2(in_2[6]), .A3(in_2[7]), .B0(in_3[4]), .B1(in_3[5]),
    .B2(in_3[6]), .B3(in_3[7]), .C1(cla_2_c1), .C2(cla_2_c2), .C3(cla_2_c3), .C4(cla_2_c4));
  CLA cla_3 (
    .C0(cla_2_c4), .A0(in_2[8]), .A1(in_2[9]), .A2(in_2[10]), .A3(in_2[11]), .B0(in_3[8]), .B1(in_3[9]),
    .B2(in_3[10]), .B3(in_3[11]), .C1(cla_3_c1), .C2(cla_3_c2), .C3(cla_3_c3), .C4(cla_3_c4));
  CLA cla_4 (
    .C0(cla_3_c4), .A0(in_2[12]), .A1(in_2[13]), .A2(in_2[14]), .A3(in_2[15]), .B0(in_3[12]), .B1(in_3[13]),
    .B2(in_3[14]), .B3(in_3[15]), .C1(cla_4_c1), .C2(cla_4_c2), .C3(cla_4_c3), .C4(Cout));
  _1_bit_adder u_1_bit_adder_1 (.in_1(in_2[0]), .in_2(in_3[0]), .cin(Cin), .s(Out_put[0]));  // open: cout
  _1_bit_adder u_1_bit_adder_2 (.in_1(in_2[1]), .in_2(in_3[1]), .cin(cla_1_c1), .s(Out_put[1]));  // open: cout
  _1_bit_adder u_1_bit_adder_3 (.in_1(in_2[2]), .in_2(in_3[2]), .cin(cla_1_c2), .s(Out_put[2]));  // open: cout
  _1_bit_adder u_1_bit_adder_4 (.in_1(in_2[3]), .in_2(in_3[3]), .cin(cla_1_c3), .s(Out_put[3]));  // open: cout
  _1_bit_adder u_1_bit_adder_5 (.in_1(in_2[4]), .in_2(in_3[4]), .cin(cla_1_c4), .s(Out_put[4]));  // open: cout
  _1_bit_adder u_1_bit_adder_6 (.in_1(in_2[5]), .in_2(in_3[5]), .cin(cla_2_c1), .s(Out_put[5]));  // open: cout
  _1_bit_adder u_1_bit_adder_7 (.in_1(in_2[6]), .in_2(in_3[6]), .cin(cla_2_c2), .s(Out_put[6]));  // open: cout
  _1_bit_adder u_1_bit_adder_8 (.in_1(in_2[7]), .in_2(in_3[7]), .cin(cla_2_c3), .s(Out_put[7]));  // open: cout
  _1_bit_adder u_1_bit_adder_9 (.in_1(in_2[8]), .in_2(in_3[8]), .cin(cla_2_c4), .s(Out_put[8]));  // open: cout
  _1_bit_adder u_1_bit_adder_10 (.in_1(in_2[9]), .in_2(in_3[9]), .cin(cla_3_c1), .s(Out_put[9]));  // open: cout
  _1_bit_adder u_1_bit_adder_11 (.in_1(in_2[10]), .in_2(in_3[10]), .cin(cla_3_c2), .s(Out_put[10]));  // open: cout
  _1_bit_adder u_1_bit_adder_12 (.in_1(in_2[11]), .in_2(in_3[11]), .cin(cla_3_c3), .s(Out_put[11]));  // open: cout
  _1_bit_adder u_1_bit_adder_13 (.in_1(in_2[12]), .in_2(in_3[12]), .cin(cla_3_c4), .s(Out_put[12]));  // open: cout
  _1_bit_adder u_1_bit_adder_14 (.in_1(in_2[13]), .in_2(in_3[13]), .cin(cla_4_c1), .s(Out_put[13]));  // open: cout
  _1_bit_adder u_1_bit_adder_15 (.in_1(in_2[14]), .in_2(in_3[14]), .cin(cla_4_c2), .s(Out_put[14]));  // open: cout
  _1_bit_adder u_1_bit_adder_16 (.in_1(in_2[15]), .in_2(in_3[15]), .cin(cla_4_c3), .s(Out_put[15]));  // open: cout

  // Notes on the sheet:
  //   B
  //   16 Bit CLA
  //   ASIF MAHMUD
  //   A
  //   1
  //   2
  //   3
  //   4
  //   5
  //   6
  //   7
  //   8
  //   9
  //   10
  //   11
  //   12
  //   13
  //   14
  //   15
  //   16
endmodule

module _16_x_16_Multiplier (
  input  [15:0] INPUT_1,
  input  [15:0] INPUT_2,
  output [15:0] out_3,
  output Z11,
  output Z12,
  output Z13,
  output Z14,
  output Z15,
  output Z16,
  output Z17,
  output Z18,
  output Z19,
  output Z20,
  output Z21,
  output Z22,
  output Z23,
  output Z24,
  output Z25,
  output Z26,
  output Z27,
  output Z28,
  output Z29,
  output Z30,
  output Z31
);

  wire adder_1_cout, adder_1_out, adder_2_cout, adder_2_out, adder_3_cout, adder_3_out, adder_4_cout,
       adder_4_out, adder_5_cout, adder_5_out, adder_6_cout, adder_6_out, adder_7_cout, adder_7_out,
       adder_8_cout, adder_8_out, adder_9_cout, adder_9_out, adder_10_cout, adder_10_out, adder_11_cout,
       adder_11_out, adder_12_cout, adder_12_out, adder_13_cout, adder_13_out, adder_14_cout, adder_14_out,
       adder_15_cout, adder_15_out, adder_16_cout, adder_16_out, adder_17_cout, adder_17_out, adder_18_cout,
       adder_18_out, adder_19_cout, adder_19_out, adder_20_cout, adder_20_out, adder_21_cout, adder_21_out,
       adder_22_cout, adder_22_out, adder_23_cout, adder_23_out, adder_24_cout, adder_24_out, adder_25_cout,
       adder_25_out, adder_26_cout, adder_26_out, adder_27_cout, adder_27_out, adder_28_cout, adder_28_out,
       adder_29_cout, adder_29_out, adder_30_cout, adder_30_out, adder_32_cout, adder_32_out, adder_33_cout,
       adder_33_out, adder_34_cout, adder_34_out, adder_35_cout, adder_35_out, adder_36_cout, adder_36_out,
       adder_37_cout, adder_37_out, adder_38_cout, adder_38_out, adder_39_cout, adder_39_out, adder_40_cout,
       adder_40_out, adder_41_cout, adder_41_out, adder_42_cout, adder_42_out, adder_43_cout, adder_43_out,
       adder_44_cout, adder_44_out, adder_45_cout, adder_45_out, adder_46_cout, adder_47_cout, adder_47_out,
       adder_48_cout, adder_48_out, adder_49_cout, adder_49_out, adder_50_cout, adder_50_out, adder_51_cout,
       adder_51_out, adder_52_cout, adder_52_out, adder_53_cout, adder_53_out, adder_54_cout, adder_54_out,
       adder_55_cout, adder_55_out, adder_56_cout, adder_56_out, adder_57_cout, adder_57_out, adder_58_cout,
       adder_58_out, adder_59_cout, adder_59_out, adder_60_cout, adder_60_out, adder_61_cout, adder_61_out,
       adder_62_cout, adder_62_out, adder_63_cout, adder_63_out, adder_64_cout, adder_64_out, adder_65_cout,
       adder_65_out, adder_66_cout, adder_66_out, adder_67_cout, adder_67_out, adder_68_cout, adder_68_out,
       adder_69_cout, adder_69_out, adder_70_cout, adder_70_out, adder_71_cout, adder_71_out, adder_72_cout,
       adder_73_cout, adder_73_out, adder_74_cout, adder_74_out, adder_75_cout, adder_75_out, adder_76_cout,
       adder_76_out, adder_77_cout, adder_77_out, adder_78_cout, adder_78_out, adder_79_cout, adder_79_out,
       adder_80_cout, adder_80_out, adder_81_cout, adder_81_out, adder_82_cout, adder_82_out, adder_83_cout,
       adder_83_out, adder_84_cout, adder_84_out, adder_85_cout, adder_85_out, adder_86_cout, adder_87_cout,
       adder_87_out, adder_88_cout, adder_88_out, adder_89_cout, adder_89_out, adder_90_cout, adder_90_out,
       adder_91_cout, adder_91_out, adder_92_cout, adder_92_out, adder_93_cout, adder_93_out, adder_94_cout,
       adder_94_out, adder_95_cout, adder_95_out, adder_96_cout, adder_96_out, adder_97_cout, adder_97_out,
       adder_98_cout, adder_98_out, adder_99_cout, adder_100_cout, adder_100_out, adder_101_cout,
       adder_101_out, adder_102_cout, adder_102_out, adder_103_cout, adder_103_out, adder_104_cout,
       adder_104_out, adder_105_cout, adder_105_out, adder_106_cout, adder_106_out, adder_107_cout,
       adder_107_out, adder_108_cout, adder_108_out, adder_109_cout, adder_109_out, adder_110_cout,
       adder_110_out, adder_111_cout, adder_112_cout, adder_112_out, adder_113_cout, adder_113_out,
       adder_114_cout, adder_114_out, adder_115_cout, adder_115_out, adder_116_cout, adder_116_out,
       adder_117_cout, adder_117_out, adder_118_cout, adder_118_out, adder_119_cout, adder_119_out,
       adder_120_cout, adder_120_out, adder_121_cout, adder_121_out, adder_122_cout, adder_122_out,
       adder_123_cout, adder_123_out, adder_124_cout, adder_124_out, adder_125_cout, adder_126_cout,
       adder_126_out, adder_127_cout, adder_127_out, adder_128_cout, adder_128_out, adder_129_cout,
       adder_129_out, adder_130_cout, adder_130_out, adder_131_cout, adder_131_out, adder_132_cout,
       adder_132_out, adder_133_cout, adder_133_out, adder_134_cout, adder_134_out, adder_135_cout,
       adder_135_out, adder_136_cout, adder_136_out, adder_137_cout, adder_137_out, adder_138_cout,
       adder_138_out, adder_139_cout, adder_140_cout, adder_140_out, adder_141_cout, adder_141_out,
       adder_142_cout, adder_142_out, adder_143_cout, adder_143_out, adder_144_cout, adder_144_out,
       adder_145_cout, adder_145_out, adder_146_cout, adder_146_out, adder_147_cout, adder_147_out,
       adder_148_cout, adder_148_out, adder_149_cout, adder_149_out, adder_150_cout, adder_150_out,
       adder_151_cout, adder_151_out, adder_152_cout, adder_152_out, adder_153_cout, adder_154_cout,
       adder_154_out, adder_155_cout, adder_155_out, adder_156_cout, adder_156_out, adder_157_cout,
       adder_157_out, adder_158_cout, adder_158_out, adder_159_cout, adder_159_out, adder_160_cout,
       adder_160_out, adder_161_cout, adder_161_out, adder_162_cout, adder_162_out, adder_163_cout,
       adder_163_out, adder_164_cout, adder_164_out, adder_165_cout, adder_166_cout, adder_166_out,
       adder_167_cout, adder_167_out, adder_168_cout, adder_168_out, adder_169_cout, adder_169_out,
       adder_170_cout, adder_170_out, adder_171_cout, adder_171_out, adder_172_cout, adder_172_out,
       adder_173_cout, adder_173_out, adder_174_cout, adder_174_out, adder_175_cout, adder_175_out,
       adder_176_cout, adder_176_out, adder_177_cout, adder_177_out, adder_178_cout, adder_178_out,
       adder_179_cout, adder_179_out, adder_180_cout, adder_181_cout, adder_181_out, adder_182_cout,
       adder_182_out, adder_183_cout, adder_183_out, adder_184_cout, adder_184_out, adder_185_cout,
       adder_185_out, adder_186_cout, adder_186_out, adder_187_cout, adder_187_out, adder_188_cout,
       adder_188_out, adder_189_cout, adder_189_out, adder_190_cout, adder_190_out, adder_191_cout,
       adder_191_out, adder_192_cout, adder_192_out, adder_193_cout, adder_193_out, adder_194_cout,
       adder_194_out, adder_195_cout, adder_195_out, adder_196_cout, adder_196_out, adder_197_cout,
       adder_197_out, adder_198_cout, adder_198_out, adder_199_cout, adder_199_out, adder_200_cout,
       adder_200_out, adder_201_cout, adder_201_out, adder_202_cout, adder_202_out, adder_203_cout,
       adder_203_out, adder_204_cout, adder_204_out, adder_205_cout, adder_205_out, adder_206_cout,
       adder_207_cout, adder_208_cout, adder_209_cout, adder_210_cout, adder_211_cout, adder_211_out,
       adder_212_cout, adder_212_out, adder_213_cout, adder_213_out, adder_214_cout, adder_214_out,
       adder_215_cout, adder_215_out, adder_216_cout, adder_216_out, adder_217_cout, adder_217_out,
       adder_218_cout, adder_218_out, adder_219_cout, adder_220_cout, adder_221_cout, adder_222_cout,
       adder_223_cout, adder_223_out, adder_224_cout, adder_224_out, adder_225_cout, adder_225_out,
       adder_226_cout, adder_226_out, adder_227_cout, adder_227_out, adder_228_cout, adder_229_cout,
       adder_230_cout, adder_231_cout, adder_232_cout, adder_233_cout, adder_233_out, adder_234_cout,
       adder_234_out, adder_235_cout, adder_235_out, adder_236_cout, adder_237_cout, adder_238_cout,
       adder_239_cout, adder_240_cout, and_1_out, and_2_out, and_3_out, and_4_out, and_5_out, and_6_out,
       and_7_out, and_8_out, and_9_out, and_10_out, and_11_out, and_12_out, and_13_out, and_14_out,
       and_15_out, and_16_out, and_17_out, and_18_out, and_19_out, and_20_out, and_21_out, and_22_out,
       and_23_out, and_24_out, and_25_out, and_26_out, and_27_out, and_28_out, and_29_out, and_30_out,
       and_31_out, and_32_out, and_33_out, and_34_out, and_35_out, and_36_out, and_37_out, and_38_out,
       and_39_out, and_40_out, and_41_out, and_42_out, and_43_out, and_44_out, and_45_out, and_46_out,
       and_47_out, and_48_out, and_49_out, and_50_out, and_51_out, and_52_out, and_53_out, and_54_out,
       and_55_out, and_56_out, and_57_out, and_58_out, and_59_out, and_60_out, and_61_out, and_62_out,
       and_63_out, and_64_out, and_65_out, and_66_out, and_67_out, and_68_out, and_69_out, and_70_out,
       and_71_out, and_72_out, and_73_out, and_74_out, and_75_out, and_76_out, and_77_out, and_78_out,
       and_79_out, and_80_out, and_81_out, and_82_out, and_83_out, and_84_out, and_85_out, and_86_out,
       and_87_out, and_88_out, and_89_out, and_90_out, and_91_out, and_92_out, and_93_out, and_94_out,
       and_95_out, and_96_out, and_97_out, and_98_out, and_99_out, and_100_out, and_101_out, and_102_out,
       and_103_out, and_104_out, and_105_out, and_106_out, and_107_out, and_108_out, and_109_out,
       and_110_out, and_111_out, and_112_out, and_113_out, and_114_out, and_115_out, and_116_out,
       and_117_out, and_118_out, and_119_out, and_120_out, and_121_out, and_122_out, and_123_out,
       and_124_out, and_125_out, and_126_out, and_127_out, and_128_out, and_129_out, and_130_out,
       and_131_out, and_132_out, and_133_out, and_134_out, and_135_out, and_136_out, and_137_out,
       and_138_out, and_139_out, and_140_out, and_141_out, and_142_out, and_143_out, and_144_out,
       and_145_out, and_146_out, and_147_out, and_148_out, and_149_out, and_150_out, and_151_out,
       and_152_out, and_153_out, and_154_out, and_155_out, and_156_out, and_157_out, and_158_out,
       and_159_out, and_160_out, and_161_out, and_162_out, and_163_out, and_164_out, and_165_out,
       and_166_out, and_167_out, and_168_out, and_169_out, and_170_out, and_171_out, and_172_out,
       and_173_out, and_174_out, and_175_out, and_176_out, and_177_out, and_178_out, and_179_out,
       and_180_out, and_181_out, and_182_out, and_183_out, and_184_out, and_185_out, and_186_out,
       and_187_out, and_188_out, and_189_out, and_190_out, and_191_out, and_192_out, and_193_out,
       and_194_out, and_195_out, and_196_out, and_197_out, and_198_out, and_199_out, and_200_out,
       and_201_out, and_202_out, and_203_out, and_204_out, and_205_out, and_206_out, and_207_out,
       and_208_out, and_209_out, and_210_out, and_211_out, and_212_out, and_213_out, and_214_out,
       and_215_out, and_216_out, and_217_out, and_218_out, and_219_out, and_220_out, and_221_out,
       and_222_out, and_223_out, and_224_out, and_225_out, and_226_out, and_227_out, and_228_out,
       and_230_out, and_231_out, and_232_out, and_233_out, and_234_out, and_235_out, and_236_out,
       and_237_out, and_238_out, and_239_out, and_240_out, and_241_out, and_242_out, and_243_out,
       and_244_out, and_245_out, and_246_out, and_247_out, and_248_out, and_249_out, and_250_out,
       and_251_out, and_252_out, and_253_out, and_254_out, and_255_out, and_256_out;

  Adder #(.width(1)) adder_1 (.a(and_1_out), .b(1'b0), .out(adder_1_out), .cin(adder_4_cout), .cout(adder_1_cout));
  Adder #(.width(1)) adder_2 (
    .a(and_2_out), .b(adder_1_cout), .out(adder_2_out), .cin(adder_5_cout), .cout(adder_2_cout));
  Adder #(.width(1)) adder_3 (
    .a(and_3_out), .b(adder_2_cout), .out(adder_3_out), .cin(adder_11_cout), .cout(adder_3_cout));
  and and_1 (and_1_out, INPUT_1[15], INPUT_2[1]);
  Adder #(.width(1)) adder_4 (.a(and_6_out), .b(and_5_out), .out(adder_4_out), .cin(adder_9_cout), .cout(adder_4_cout));
  and and_2 (and_2_out, INPUT_1[15], INPUT_2[2]);
  Adder #(.width(1)) adder_5 (
    .a(and_7_out), .b(adder_1_out), .out(adder_5_out), .cin(adder_10_cout), .cout(adder_5_cout));
  and and_3 (and_3_out, INPUT_1[15], INPUT_2[3]);
  and and_4 (and_4_out, INPUT_1[15], INPUT_2[4]);
  Adder #(.width(1)) adder_6 (
    .a(and_4_out), .b(adder_3_cout), .out(adder_6_out), .cin(adder_12_cout), .cout(adder_6_cout));
  Adder #(.width(1)) adder_7 (
    .a(and_9_out), .b(adder_6_cout), .out(adder_7_out), .cin(adder_13_cout), .cout(adder_7_cout));
  Adder #(.width(1)) adder_8 (
    .a(and_10_out), .b(adder_7_cout), .out(adder_8_out), .cin(adder_14_cout), .cout(adder_8_cout));
  and and_5 (and_5_out, INPUT_1[15], INPUT_2[0]);
  and and_6 (and_6_out, INPUT_1[14], INPUT_2[1]);
  Adder #(.width(1)) adder_9 (
    .a(and_13_out), .b(and_12_out), .out(adder_9_out), .cin(adder_19_cout), .cout(adder_9_cout));
  and and_7 (and_7_out, INPUT_1[14], INPUT_2[2]);
  Adder #(.width(1)) adder_10 (
    .a(and_14_out), .b(adder_4_out), .out(adder_10_out), .cin(adder_33_cout), .cout(adder_10_cout));
  and and_8 (and_8_out, INPUT_1[14], INPUT_2[3]);
  Adder #(.width(1)) adder_11 (
    .a(and_8_out), .b(adder_2_out), .out(adder_11_out), .cin(adder_20_cout), .cout(adder_11_cout));
  Adder #(.width(1)) adder_12 (
    .a(and_16_out), .b(adder_3_out), .out(adder_12_out), .cin(adder_21_cout), .cout(adder_12_cout));
  and and_9 (and_9_out, INPUT_1[15], INPUT_2[5]);
  Adder #(.width(1)) adder_13 (
    .a(and_17_out), .b(adder_6_out), .out(adder_13_out), .cin(adder_22_cout), .cout(adder_13_cout));
  and and_10 (and_10_out, INPUT_1[15], INPUT_2[6]);
  Adder #(.width(1)) adder_14 (
    .a(and_18_out), .b(adder_7_out), .out(adder_14_out), .cin(adder_37_cout), .cout(adder_14_cout));
  and and_11 (and_11_out, INPUT_1[15], INPUT_2[7]);
  Adder #(.width(1)) adder_15 (
    .a(and_11_out), .b(adder_8_cout), .out(adder_15_out), .cin(adder_23_cout), .cout(adder_15_cout));
  Adder #(.width(1)) adder_16 (
    .a(and_19_out), .b(adder_15_cout), .out(adder_16_out), .cin(adder_24_cout), .cout(adder_16_cout));
  Adder #(.width(1)) adder_17 (
    .a(and_20_out), .b(adder_16_cout), .out(adder_17_out), .cin(adder_25_cout), .cout(adder_17_cout));
  Adder #(.width(1)) adder_18 (
    .a(and_21_out), .b(adder_17_cout), .out(adder_18_out), .cin(adder_26_cout), .cout(adder_18_cout));
  and and_12 (and_12_out, INPUT_1[14], INPUT_2[0]);
  and and_13 (and_13_out, INPUT_1[13], INPUT_2[1]);
  Adder #(.width(1)) adder_19 (
    .a(and_24_out), .b(and_23_out), .out(adder_19_out), .cin(adder_32_cout), .cout(adder_19_cout));
  and and_14 (and_14_out, INPUT_1[13], INPUT_2[2]);
  and and_15 (and_15_out, INPUT_1[13], INPUT_2[3]);
  Adder #(.width(1)) adder_20 (
    .a(and_15_out), .b(adder_5_out), .out(adder_20_out), .cin(adder_34_cout), .cout(adder_20_cout));
  and and_16 (and_16_out, INPUT_1[14], INPUT_2[4]);
  Adder #(.width(1)) adder_21 (
    .a(and_27_out), .b(adder_11_out), .out(adder_21_out), .cin(adder_35_cout), .cout(adder_21_cout));
  and and_17 (and_17_out, INPUT_1[14], INPUT_2[5]);
  Adder #(.width(1)) adder_22 (
    .a(and_28_out), .b(adder_12_out), .out(adder_22_out), .cin(adder_36_cout), .cout(adder_22_cout));
  and and_18 (and_18_out, INPUT_1[14], INPUT_2[6]);
  Adder #(.width(1)) adder_23 (
    .a(and_30_out), .b(adder_8_out), .out(adder_23_out), .cin(adder_38_cout), .cout(adder_23_cout));
  and and_19 (and_19_out, INPUT_1[15], INPUT_2[8]);
  Adder #(.width(1)) adder_24 (
    .a(and_31_out), .b(adder_15_out), .out(adder_24_out), .cin(adder_39_cout), .cout(adder_24_cout));
  and and_20 (and_20_out, INPUT_1[15], INPUT_2[9]);
  Adder #(.width(1)) adder_25 (
    .a(and_32_out), .b(adder_16_out), .out(adder_25_out), .cin(adder_40_cout), .cout(adder_25_cout));
  and and_21 (and_21_out, INPUT_1[15], INPUT_2[10]);
  Adder #(.width(1)) adder_26 (
    .a(and_33_out), .b(adder_17_out), .out(adder_26_out), .cin(adder_41_cout), .cout(adder_26_cout));
  and and_22 (and_22_out, INPUT_1[15], INPUT_2[11]);
  Adder #(.width(1)) adder_27 (
    .a(and_22_out), .b(adder_18_cout), .out(adder_27_out), .cin(adder_42_cout), .cout(adder_27_cout));
  Adder #(.width(1)) adder_28 (
    .a(and_35_out), .b(adder_27_cout), .out(adder_28_out), .cin(adder_43_cout), .cout(adder_28_cout));
  Adder #(.width(1)) adder_29 (
    .a(and_36_out), .b(adder_28_cout), .out(adder_29_out), .cin(adder_44_cout), .cout(adder_29_cout));
  Adder #(.width(1)) adder_30 (
    .a(and_37_out), .b(adder_29_cout), .out(adder_30_out), .cin(adder_45_cout), .cout(adder_30_cout));
  Adder #(.width(1)) adder_31 (.a(and_38_out), .b(adder_30_cout), .out(Z30), .cin(adder_46_cout), .cout(Z31));
  and and_23 (and_23_out, INPUT_1[13], INPUT_2[0]);
  and and_24 (and_24_out, INPUT_1[12], INPUT_2[1]);
  Adder #(.width(1)) adder_32 (
    .a(and_40_out), .b(and_39_out), .out(adder_32_out), .cin(adder_58_cout), .cout(adder_32_cout));
  and and_25 (and_25_out, INPUT_1[12], INPUT_2[2]);
  Adder #(.width(1)) adder_33 (
    .a(and_25_out), .b(adder_9_out), .out(adder_33_out), .cin(adder_47_cout), .cout(adder_33_cout));
  and and_26 (and_26_out, INPUT_1[12], INPUT_2[3]);
  Adder #(.width(1)) adder_34 (
    .a(and_26_out), .b(adder_10_out), .out(adder_34_out), .cin(adder_48_cout), .cout(adder_34_cout));
  and and_27 (and_27_out, INPUT_1[13], INPUT_2[4]);
  Adder #(.width(1)) adder_35 (
    .a(and_43_out), .b(adder_20_out), .out(adder_35_out), .cin(adder_49_cout), .cout(adder_35_cout));
  and and_28 (and_28_out, INPUT_1[13], INPUT_2[5]);
  Adder #(.width(1)) adder_36 (
    .a(and_44_out), .b(adder_21_out), .out(adder_36_out), .cin(adder_50_cout), .cout(adder_36_cout));
  and and_29 (and_29_out, INPUT_1[13], INPUT_2[6]);
  Adder #(.width(1)) adder_37 (
    .a(and_29_out), .b(adder_13_out), .out(adder_37_out), .cin(adder_51_cout), .cout(adder_37_cout));
  and and_30 (and_30_out, INPUT_1[14], INPUT_2[7]);
  Adder #(.width(1)) adder_38 (
    .a(and_46_out), .b(adder_14_out), .out(adder_38_out), .cin(adder_52_cout), .cout(adder_38_cout));
  and and_31 (and_31_out, INPUT_1[14], INPUT_2[8]);
  Adder #(.width(1)) adder_39 (
    .a(and_47_out), .b(adder_23_out), .out(adder_39_out), .cin(adder_53_cout), .cout(adder_39_cout));
  and and_32 (and_32_out, INPUT_1[14], INPUT_2[9]);
  Adder #(.width(1)) adder_40 (
    .a(and_48_out), .b(adder_24_out), .out(adder_40_out), .cin(adder_54_cout), .cout(adder_40_cout));
  and and_33 (and_33_out, INPUT_1[14], INPUT_2[10]);
  Adder #(.width(1)) adder_41 (
    .a(and_49_out), .b(adder_25_out), .out(adder_41_out), .cin(adder_67_cout), .cout(adder_41_cout));
  and and_34 (and_34_out, INPUT_1[14], INPUT_2[11]);
  Adder #(.width(1)) adder_42 (
    .a(and_34_out), .b(adder_18_out), .out(adder_42_out), .cin(adder_55_cout), .cout(adder_42_cout));
  and and_35 (and_35_out, INPUT_1[15], INPUT_2[12]);
  Adder #(.width(1)) adder_43 (
    .a(and_51_out), .b(adder_27_out), .out(adder_43_out), .cin(adder_56_cout), .cout(adder_43_cout));
  and and_36 (and_36_out, INPUT_1[15], INPUT_2[13]);
  Adder #(.width(1)) adder_44 (
    .a(and_52_out), .b(adder_28_out), .out(adder_44_out), .cin(adder_57_cout), .cout(adder_44_cout));
  and and_37 (and_37_out, INPUT_1[15], INPUT_2[14]);
  Adder #(.width(1)) adder_45 (
    .a(and_53_out), .b(adder_29_out), .out(adder_45_out), .cin(adder_71_cout), .cout(adder_45_cout));
  and and_38 (and_38_out, INPUT_1[15], INPUT_2[15]);
  Adder #(.width(1)) adder_46 (.a(and_54_out), .b(adder_30_out), .out(Z29), .cin(adder_72_cout), .cout(adder_46_cout));
  and and_39 (and_39_out, INPUT_1[12], INPUT_2[0]);
  and and_40 (and_40_out, INPUT_1[11], INPUT_2[1]);
  and and_41 (and_41_out, INPUT_1[11], INPUT_2[2]);
  Adder #(.width(1)) adder_47 (
    .a(and_41_out), .b(adder_19_out), .out(adder_47_out), .cin(adder_59_cout), .cout(adder_47_cout));
  and and_42 (and_42_out, INPUT_1[11], INPUT_2[3]);
  Adder #(.width(1)) adder_48 (
    .a(and_42_out), .b(adder_33_out), .out(adder_48_out), .cin(adder_60_cout), .cout(adder_48_cout));
  and and_43 (and_43_out, INPUT_1[12], INPUT_2[4]);
  Adder #(.width(1)) adder_49 (
    .a(and_59_out), .b(adder_34_out), .out(adder_49_out), .cin(adder_61_cout), .cout(adder_49_cout));
  and and_44 (and_44_out, INPUT_1[12], INPUT_2[5]);
  Adder #(.width(1)) adder_50 (
    .a(and_60_out), .b(adder_35_out), .out(adder_50_out), .cin(adder_62_cout), .cout(adder_50_cout));
  and and_45 (and_45_out, INPUT_1[12], INPUT_2[6]);
  Adder #(.width(1)) adder_51 (
    .a(and_45_out), .b(adder_22_out), .out(adder_51_out), .cin(adder_63_cout), .cout(adder_51_cout));
  and and_46 (and_46_out, INPUT_1[13], INPUT_2[7]);
  Adder #(.width(1)) adder_52 (
    .a(and_62_out), .b(adder_37_out), .out(adder_52_out), .cin(adder_64_cout), .cout(adder_52_cout));
  and and_47 (and_47_out, INPUT_1[13], INPUT_2[8]);
  Adder #(.width(1)) adder_53 (
    .a(and_63_out), .b(adder_38_out), .out(adder_53_out), .cin(adder_65_cout), .cout(adder_53_cout));
  and and_48 (and_48_out, INPUT_1[13], INPUT_2[9]);
  Adder #(.width(1)) adder_54 (
    .a(and_64_out), .b(adder_39_out), .out(adder_54_out), .cin(adder_66_cout), .cout(adder_54_cout));
  and and_49 (and_49_out, INPUT_1[13], INPUT_2[10]);
  and and_50 (and_50_out, INPUT_1[13], INPUT_2[11]);
  Adder #(.width(1)) adder_55 (
    .a(and_50_out), .b(adder_26_out), .out(adder_55_out), .cin(adder_68_cout), .cout(adder_55_cout));
  and and_51 (and_51_out, INPUT_1[14], INPUT_2[12]);
  Adder #(.width(1)) adder_56 (
    .a(and_67_out), .b(adder_42_out), .out(adder_56_out), .cin(adder_69_cout), .cout(adder_56_cout));
  and and_52 (and_52_out, INPUT_1[14], INPUT_2[13]);
  Adder #(.width(1)) adder_57 (
    .a(and_68_out), .b(adder_43_out), .out(adder_57_out), .cin(adder_70_cout), .cout(adder_57_cout));
  and and_53 (and_53_out, INPUT_1[14], INPUT_2[14]);
  and and_54 (and_54_out, INPUT_1[14], INPUT_2[15]);
  and and_55 (and_55_out, INPUT_1[11], INPUT_2[0]);
  and and_56 (and_56_out, INPUT_1[10], INPUT_2[1]);
  Adder #(.width(1)) adder_58 (
    .a(and_56_out), .b(and_55_out), .out(adder_58_out), .cin(adder_73_cout), .cout(adder_58_cout));
  and and_57 (and_57_out, INPUT_1[10], INPUT_2[2]);
  Adder #(.width(1)) adder_59 (
    .a(and_57_out), .b(adder_32_out), .out(adder_59_out), .cin(adder_74_cout), .cout(adder_59_cout));
  and and_58 (and_58_out, INPUT_1[10], INPUT_2[3]);
  Adder #(.width(1)) adder_60 (
    .a(and_58_out), .b(adder_47_out), .out(adder_60_out), .cin(adder_75_cout), .cout(adder_60_cout));
  and and_59 (and_59_out, INPUT_1[11], INPUT_2[4]);
  Adder #(.width(1)) adder_61 (
    .a(and_75_out), .b(adder_48_out), .out(adder_61_out), .cin(adder_76_cout), .cout(adder_61_cout));
  and and_60 (and_60_out, INPUT_1[11], INPUT_2[5]);
  Adder #(.width(1)) adder_62 (
    .a(and_76_out), .b(adder_49_out), .out(adder_62_out), .cin(adder_91_cout), .cout(adder_62_cout));
  and and_61 (and_61_out, INPUT_1[11], INPUT_2[6]);
  Adder #(.width(1)) adder_63 (
    .a(and_61_out), .b(adder_36_out), .out(adder_63_out), .cin(adder_77_cout), .cout(adder_63_cout));
  and and_62 (and_62_out, INPUT_1[12], INPUT_2[7]);
  Adder #(.width(1)) adder_64 (
    .a(and_78_out), .b(adder_51_out), .out(adder_64_out), .cin(adder_78_cout), .cout(adder_64_cout));
  and and_63 (and_63_out, INPUT_1[12], INPUT_2[8]);
  Adder #(.width(1)) adder_65 (
    .a(and_79_out), .b(adder_52_out), .out(adder_65_out), .cin(adder_79_cout), .cout(adder_65_cout));
  and and_64 (and_64_out, INPUT_1[12], INPUT_2[9]);
  Adder #(.width(1)) adder_66 (
    .a(and_80_out), .b(adder_53_out), .out(adder_66_out), .cin(adder_80_cout), .cout(adder_66_cout));
  and and_65 (and_65_out, INPUT_1[12], INPUT_2[10]);
  Adder #(.width(1)) adder_67 (
    .a(and_65_out), .b(adder_40_out), .out(adder_67_out), .cin(adder_81_cout), .cout(adder_67_cout));
  and and_66 (and_66_out, INPUT_1[12], INPUT_2[11]);
  Adder #(.width(1)) adder_68 (
    .a(and_66_out), .b(adder_41_out), .out(adder_68_out), .cin(adder_82_cout), .cout(adder_68_cout));
  and and_67 (and_67_out, INPUT_1[13], INPUT_2[12]);
  Adder #(.width(1)) adder_69 (
    .a(and_83_out), .b(adder_55_out), .out(adder_69_out), .cin(adder_83_cout), .cout(adder_69_cout));
  and and_68 (and_68_out, INPUT_1[13], INPUT_2[13]);
  Adder #(.width(1)) adder_70 (
    .a(and_84_out), .b(adder_56_out), .out(adder_70_out), .cin(adder_84_cout), .cout(adder_70_cout));
  and and_69 (and_69_out, INPUT_1[13], INPUT_2[14]);
  Adder #(.width(1)) adder_71 (
    .a(and_69_out), .b(adder_44_out), .out(adder_71_out), .cin(adder_85_cout), .cout(adder_71_cout));
  and and_70 (and_70_out, INPUT_1[13], INPUT_2[15]);
  Adder #(.width(1)) adder_72 (.a(and_70_out), .b(adder_45_out), .out(Z28), .cin(adder_86_cout), .cout(adder_72_cout));
  and and_71 (and_71_out, INPUT_1[10], INPUT_2[0]);
  and and_72 (and_72_out, INPUT_1[9], INPUT_2[1]);
  Adder #(.width(1)) adder_73 (
    .a(and_72_out), .b(and_71_out), .out(adder_73_out), .cin(adder_87_cout), .cout(adder_73_cout));
  and and_73 (and_73_out, INPUT_1[9], INPUT_2[2]);
  Adder #(.width(1)) adder_74 (
    .a(and_73_out), .b(adder_58_out), .out(adder_74_out), .cin(adder_88_cout), .cout(adder_74_cout));
  and and_74 (and_74_out, INPUT_1[9], INPUT_2[3]);
  Adder #(.width(1)) adder_75 (
    .a(and_74_out), .b(adder_59_out), .out(adder_75_out), .cin(adder_89_cout), .cout(adder_75_cout));
  and and_75 (and_75_out, INPUT_1[10], INPUT_2[4]);
  Adder #(.width(1)) adder_76 (
    .a(and_91_out), .b(adder_60_out), .out(adder_76_out), .cin(adder_90_cout), .cout(adder_76_cout));
  and and_76 (and_76_out, INPUT_1[10], INPUT_2[5]);
  and and_77 (and_77_out, INPUT_1[10], INPUT_2[6]);
  Adder #(.width(1)) adder_77 (
    .a(and_77_out), .b(adder_50_out), .out(adder_77_out), .cin(adder_92_cout), .cout(adder_77_cout));
  and and_78 (and_78_out, INPUT_1[11], INPUT_2[7]);
  Adder #(.width(1)) adder_78 (
    .a(and_94_out), .b(adder_63_out), .out(adder_78_out), .cin(adder_93_cout), .cout(adder_78_cout));
  and and_79 (and_79_out, INPUT_1[11], INPUT_2[8]);
  Adder #(.width(1)) adder_79 (
    .a(and_95_out), .b(adder_64_out), .out(adder_79_out), .cin(adder_94_cout), .cout(adder_79_cout));
  and and_80 (and_80_out, INPUT_1[11], INPUT_2[9]);
  Adder #(.width(1)) adder_80 (
    .a(and_96_out), .b(adder_65_out), .out(adder_80_out), .cin(adder_106_cout), .cout(adder_80_cout));
  and and_81 (and_81_out, INPUT_1[11], INPUT_2[10]);
  Adder #(.width(1)) adder_81 (
    .a(and_81_out), .b(adder_54_out), .out(adder_81_out), .cin(adder_95_cout), .cout(adder_81_cout));
  and and_82 (and_82_out, INPUT_1[11], INPUT_2[11]);
  Adder #(.width(1)) adder_82 (
    .a(and_82_out), .b(adder_67_out), .out(adder_82_out), .cin(adder_96_cout), .cout(adder_82_cout));
  and and_83 (and_83_out, INPUT_1[12], INPUT_2[12]);
  Adder #(.width(1)) adder_83 (
    .a(and_99_out), .b(adder_68_out), .out(adder_83_out), .cin(adder_97_cout), .cout(adder_83_cout));
  and and_84 (and_84_out, INPUT_1[12], INPUT_2[13]);
  Adder #(.width(1)) adder_84 (
    .a(and_100_out), .b(adder_69_out), .out(adder_84_out), .cin(adder_109_cout), .cout(adder_84_cout));
  and and_85 (and_85_out, INPUT_1[12], INPUT_2[14]);
  Adder #(.width(1)) adder_85 (
    .a(and_85_out), .b(adder_57_out), .out(adder_85_out), .cin(adder_98_cout), .cout(adder_85_cout));
  and and_86 (and_86_out, INPUT_1[12], INPUT_2[15]);
  Adder #(.width(1)) adder_86 (.a(and_86_out), .b(adder_71_out), .out(Z27), .cin(adder_99_cout), .cout(adder_86_cout));
  and and_87 (and_87_out, INPUT_1[9], INPUT_2[0]);
  and and_88 (and_88_out, INPUT_1[8], INPUT_2[1]);
  Adder #(.width(1)) adder_87 (
    .a(and_88_out), .b(and_87_out), .out(adder_87_out), .cin(adder_100_cout), .cout(adder_87_cout));
  and and_89 (and_89_out, INPUT_1[8], INPUT_2[2]);
  Adder #(.width(1)) adder_88 (
    .a(and_89_out), .b(adder_73_out), .out(adder_88_out), .cin(adder_101_cout), .cout(adder_88_cout));
  and and_90 (and_90_out, INPUT_1[8], INPUT_2[3]);
  Adder #(.width(1)) adder_89 (
    .a(and_90_out), .b(adder_74_out), .out(adder_89_out), .cin(adder_102_cout), .cout(adder_89_cout));
  and and_91 (and_91_out, INPUT_1[9], INPUT_2[4]);
  Adder #(.width(1)) adder_90 (
    .a(and_107_out), .b(adder_75_out), .out(adder_90_out), .cin(adder_115_cout), .cout(adder_90_cout));
  and and_92 (and_92_out, INPUT_1[9], INPUT_2[5]);
  Adder #(.width(1)) adder_91 (
    .a(and_92_out), .b(adder_61_out), .out(adder_91_out), .cin(adder_103_cout), .cout(adder_91_cout));
  and and_93 (and_93_out, INPUT_1[9], INPUT_2[6]);
  Adder #(.width(1)) adder_92 (
    .a(and_93_out), .b(adder_62_out), .out(adder_92_out), .cin(adder_104_cout), .cout(adder_92_cout));
  and and_94 (and_94_out, INPUT_1[10], INPUT_2[7]);
  Adder #(.width(1)) adder_93 (
    .a(and_110_out), .b(adder_77_out), .out(adder_93_out), .cin(adder_105_cout), .cout(adder_93_cout));
  and and_95 (and_95_out, INPUT_1[10], INPUT_2[8]);
  Adder #(.width(1)) adder_94 (
    .a(and_111_out), .b(adder_78_out), .out(adder_94_out), .cin(adder_118_cout), .cout(adder_94_cout));
  and and_96 (and_96_out, INPUT_1[10], INPUT_2[9]);
  and and_97 (and_97_out, INPUT_1[10], INPUT_2[10]);
  Adder #(.width(1)) adder_95 (
    .a(and_97_out), .b(adder_66_out), .out(adder_95_out), .cin(adder_107_cout), .cout(adder_95_cout));
  and and_98 (and_98_out, INPUT_1[10], INPUT_2[11]);
  Adder #(.width(1)) adder_96 (
    .a(and_98_out), .b(adder_81_out), .out(adder_96_out), .cin(adder_108_cout), .cout(adder_96_cout));
  and and_99 (and_99_out, INPUT_1[11], INPUT_2[12]);
  Adder #(.width(1)) adder_97 (
    .a(and_115_out), .b(adder_82_out), .out(adder_97_out), .cin(adder_122_cout), .cout(adder_97_cout));
  and and_100 (and_100_out, INPUT_1[11], INPUT_2[13]);
  and and_101 (and_101_out, INPUT_1[11], INPUT_2[14]);
  Adder #(.width(1)) adder_98 (
    .a(and_101_out), .b(adder_70_out), .out(adder_98_out), .cin(adder_110_cout), .cout(adder_98_cout));
  and and_102 (and_102_out, INPUT_1[11], INPUT_2[15]);
  Adder #(.width(1)) adder_99 (
    .a(and_102_out), .b(adder_85_out), .out(Z26), .cin(adder_111_cout), .cout(adder_99_cout));
  and and_103 (and_103_out, INPUT_1[8], INPUT_2[0]);
  and and_104 (and_104_out, INPUT_1[7], INPUT_2[1]);
  Adder #(.width(1)) adder_100 (
    .a(and_104_out), .b(and_103_out), .out(adder_100_out), .cin(adder_112_cout), .cout(adder_100_cout));
  and and_105 (and_105_out, INPUT_1[7], INPUT_2[2]);
  Adder #(.width(1)) adder_101 (
    .a(and_105_out), .b(adder_87_out), .out(adder_101_out), .cin(adder_113_cout), .cout(adder_101_cout));
  and and_106 (and_106_out, INPUT_1[7], INPUT_2[3]);
  Adder #(.width(1)) adder_102 (
    .a(and_106_out), .b(adder_88_out), .out(adder_102_out), .cin(adder_114_cout), .cout(adder_102_cout));
  and and_107 (and_107_out, INPUT_1[8], INPUT_2[4]);
  and and_108 (and_108_out, INPUT_1[8], INPUT_2[5]);
  Adder #(.width(1)) adder_103 (
    .a(and_108_out), .b(adder_76_out), .out(adder_103_out), .cin(adder_116_cout), .cout(adder_103_cout));
  and and_109 (and_109_out, INPUT_1[8], INPUT_2[6]);
  Adder #(.width(1)) adder_104 (
    .a(and_109_out), .b(adder_91_out), .out(adder_104_out), .cin(adder_117_cout), .cout(adder_104_cout));
  and and_110 (and_110_out, INPUT_1[9], INPUT_2[7]);
  Adder #(.width(1)) adder_105 (
    .a(and_125_out), .b(adder_92_out), .out(adder_105_out), .cin(adder_131_cout), .cout(adder_105_cout));
  and and_111 (and_111_out, INPUT_1[9], INPUT_2[8]);
  and and_112 (and_112_out, INPUT_1[9], INPUT_2[9]);
  Adder #(.width(1)) adder_106 (
    .a(and_112_out), .b(adder_79_out), .out(adder_106_out), .cin(adder_119_cout), .cout(adder_106_cout));
  and and_113 (and_113_out, INPUT_1[9], INPUT_2[10]);
  Adder #(.width(1)) adder_107 (
    .a(and_113_out), .b(adder_80_out), .out(adder_107_out), .cin(adder_120_cout), .cout(adder_107_cout));
  and and_114 (and_114_out, INPUT_1[9], INPUT_2[11]);
  Adder #(.width(1)) adder_108 (
    .a(and_114_out), .b(adder_95_out), .out(adder_108_out), .cin(adder_121_cout), .cout(adder_108_cout));
  and and_115 (and_115_out, INPUT_1[10], INPUT_2[12]);
  and and_116 (and_116_out, INPUT_1[10], INPUT_2[13]);
  Adder #(.width(1)) adder_109 (
    .a(and_116_out), .b(adder_83_out), .out(adder_109_out), .cin(adder_123_cout), .cout(adder_109_cout));
  and and_117 (and_117_out, INPUT_1[10], INPUT_2[14]);
  Adder #(.width(1)) adder_110 (
    .a(and_117_out), .b(adder_84_out), .out(adder_110_out), .cin(adder_124_cout), .cout(adder_110_cout));
  and and_118 (and_118_out, INPUT_1[10], INPUT_2[15]);
  Adder #(.width(1)) adder_111 (
    .a(and_118_out), .b(adder_98_out), .out(Z25), .cin(adder_125_cout), .cout(adder_111_cout));
  and and_119 (and_119_out, INPUT_1[7], INPUT_2[0]);
  and and_120 (and_120_out, INPUT_1[6], INPUT_2[1]);
  Adder #(.width(1)) adder_112 (
    .a(and_120_out), .b(and_119_out), .out(adder_112_out), .cin(adder_126_cout), .cout(adder_112_cout));
  and and_121 (and_121_out, INPUT_1[6], INPUT_2[2]);
  Adder #(.width(1)) adder_113 (
    .a(and_121_out), .b(adder_100_out), .out(adder_113_out), .cin(adder_127_cout), .cout(adder_113_cout));
  Adder #(.width(1)) adder_114 (
    .a(and_137_out), .b(adder_101_out), .out(adder_114_out), .cin(adder_142_cout), .cout(adder_114_cout));
  and and_122 (and_122_out, INPUT_1[7], INPUT_2[4]);
  Adder #(.width(1)) adder_115 (
    .a(and_122_out), .b(adder_89_out), .out(adder_115_out), .cin(adder_128_cout), .cout(adder_115_cout));
  and and_123 (and_123_out, INPUT_1[7], INPUT_2[5]);
  Adder #(.width(1)) adder_116 (
    .a(and_123_out), .b(adder_90_out), .out(adder_116_out), .cin(adder_129_cout), .cout(adder_116_cout));
  and and_124 (and_124_out, INPUT_1[7], INPUT_2[6]);
  Adder #(.width(1)) adder_117 (
    .a(and_124_out), .b(adder_103_out), .out(adder_117_out), .cin(adder_130_cout), .cout(adder_117_cout));
  and and_125 (and_125_out, INPUT_1[8], INPUT_2[7]);
  and and_126 (and_126_out, INPUT_1[8], INPUT_2[8]);
  Adder #(.width(1)) adder_118 (
    .a(and_126_out), .b(adder_93_out), .out(adder_118_out), .cin(adder_132_cout), .cout(adder_118_cout));
  and and_127 (and_127_out, INPUT_1[8], INPUT_2[9]);
  Adder #(.width(1)) adder_119 (
    .a(and_127_out), .b(adder_94_out), .out(adder_119_out), .cin(adder_133_cout), .cout(adder_119_cout));
  and and_128 (and_128_out, INPUT_1[8], INPUT_2[10]);
  Adder #(.width(1)) adder_120 (
    .a(and_128_out), .b(adder_106_out), .out(adder_120_out), .cin(adder_134_cout), .cout(adder_120_cout));
  and and_129 (and_129_out, INPUT_1[8], INPUT_2[11]);
  Adder #(.width(1)) adder_121 (
    .a(and_129_out), .b(adder_107_out), .out(adder_121_out), .cin(adder_135_cout), .cout(adder_121_cout));
  and and_130 (and_130_out, INPUT_1[9], INPUT_2[12]);
  Adder #(.width(1)) adder_122 (
    .a(and_130_out), .b(adder_96_out), .out(adder_122_out), .cin(adder_136_cout), .cout(adder_122_cout));
  and and_131 (and_131_out, INPUT_1[9], INPUT_2[13]);
  Adder #(.width(1)) adder_123 (
    .a(and_131_out), .b(adder_97_out), .out(adder_123_out), .cin(adder_137_cout), .cout(adder_123_cout));
  and and_132 (and_132_out, INPUT_1[9], INPUT_2[14]);
  Adder #(.width(1)) adder_124 (
    .a(and_132_out), .b(adder_109_out), .out(adder_124_out), .cin(adder_138_cout), .cout(adder_124_cout));
  and and_133 (and_133_out, INPUT_1[9], INPUT_2[15]);
  Adder #(.width(1)) adder_125 (
    .a(and_133_out), .b(adder_110_out), .out(Z24), .cin(adder_139_cout), .cout(adder_125_cout));
  and and_134 (and_134_out, INPUT_1[6], INPUT_2[0]);
  and and_135 (and_135_out, INPUT_1[5], INPUT_2[1]);
  Adder #(.width(1)) adder_126 (
    .a(and_135_out), .b(and_134_out), .out(adder_126_out), .cin(adder_140_cout), .cout(adder_126_cout));
  and and_136 (and_136_out, INPUT_1[5], INPUT_2[2]);
  Adder #(.width(1)) adder_127 (
    .a(and_136_out), .b(adder_112_out), .out(adder_127_out), .cin(adder_141_cout), .cout(adder_127_cout));
  and and_137 (and_137_out, INPUT_1[6], INPUT_2[3]);
  and and_138 (and_138_out, INPUT_1[6], INPUT_2[4]);
  Adder #(.width(1)) adder_128 (
    .a(and_138_out), .b(adder_102_out), .out(adder_128_out), .cin(adder_143_cout), .cout(adder_128_cout));
  and and_139 (and_139_out, INPUT_1[6], INPUT_2[5]);
  Adder #(.width(1)) adder_129 (
    .a(and_139_out), .b(adder_115_out), .out(adder_129_out), .cin(adder_144_cout), .cout(adder_129_cout));
  and and_140 (and_140_out, INPUT_1[6], INPUT_2[6]);
  Adder #(.width(1)) adder_130 (
    .a(and_140_out), .b(adder_116_out), .out(adder_130_out), .cin(adder_145_cout), .cout(adder_130_cout));
  and and_141 (and_141_out, INPUT_1[7], INPUT_2[7]);
  Adder #(.width(1)) adder_131 (
    .a(and_141_out), .b(adder_104_out), .out(adder_131_out), .cin(adder_146_cout), .cout(adder_131_cout));
  and and_142 (and_142_out, INPUT_1[7], INPUT_2[8]);
  Adder #(.width(1)) adder_132 (
    .a(and_142_out), .b(adder_105_out), .out(adder_132_out), .cin(adder_147_cout), .cout(adder_132_cout));
  and and_143 (and_143_out, INPUT_1[7], INPUT_2[9]);
  Adder #(.width(1)) adder_133 (
    .a(and_143_out), .b(adder_118_out), .out(adder_133_out), .cin(adder_148_cout), .cout(adder_133_cout));
  and and_144 (and_144_out, INPUT_1[7], INPUT_2[10]);
  Adder #(.width(1)) adder_134 (
    .a(and_144_out), .b(adder_119_out), .out(adder_134_out), .cin(adder_149_cout), .cout(adder_134_cout));
  Adder #(.width(1)) adder_135 (
    .a(and_160_out), .b(adder_120_out), .out(adder_135_out), .cin(adder_161_cout), .cout(adder_135_cout));
  and and_145 (and_145_out, INPUT_1[8], INPUT_2[12]);
  Adder #(.width(1)) adder_136 (
    .a(and_145_out), .b(adder_108_out), .out(adder_136_out), .cin(adder_150_cout), .cout(adder_136_cout));
  and and_146 (and_146_out, INPUT_1[8], INPUT_2[13]);
  Adder #(.width(1)) adder_137 (
    .a(and_146_out), .b(adder_122_out), .out(adder_137_out), .cin(adder_151_cout), .cout(adder_137_cout));
  and and_147 (and_147_out, INPUT_1[8], INPUT_2[14]);
  Adder #(.width(1)) adder_138 (
    .a(and_147_out), .b(adder_123_out), .out(adder_138_out), .cin(adder_152_cout), .cout(adder_138_cout));
  and and_148 (and_148_out, INPUT_1[8], INPUT_2[15]);
  Adder #(.width(1)) adder_139 (
    .a(and_148_out), .b(adder_124_out), .out(Z23), .cin(adder_153_cout), .cout(adder_139_cout));
  and and_149 (and_149_out, INPUT_1[5], INPUT_2[0]);
  and and_150 (and_150_out, INPUT_1[4], INPUT_2[1]);
  Adder #(.width(1)) adder_140 (
    .a(and_150_out), .b(and_149_out), .out(adder_140_out), .cin(adder_166_cout), .cout(adder_140_cout));
  and and_151 (and_151_out, INPUT_1[4], INPUT_2[2]);
  Adder #(.width(1)) adder_141 (
    .a(and_151_out), .b(adder_126_out), .out(adder_141_out), .cin(adder_167_cout), .cout(adder_141_cout));
  and and_152 (and_152_out, INPUT_1[5], INPUT_2[3]);
  Adder #(.width(1)) adder_142 (
    .a(and_152_out), .b(adder_113_out), .out(adder_142_out), .cin(adder_154_cout), .cout(adder_142_cout));
  and and_153 (and_153_out, INPUT_1[5], INPUT_2[4]);
  Adder #(.width(1)) adder_143 (
    .a(and_153_out), .b(adder_114_out), .out(adder_143_out), .cin(adder_155_cout), .cout(adder_143_cout));
  and and_154 (and_154_out, INPUT_1[5], INPUT_2[5]);
  Adder #(.width(1)) adder_144 (
    .a(and_154_out), .b(adder_128_out), .out(adder_144_out), .cin(adder_156_cout), .cout(adder_144_cout));
  and and_155 (and_155_out, INPUT_1[5], INPUT_2[6]);
  Adder #(.width(1)) adder_145 (
    .a(and_155_out), .b(adder_129_out), .out(adder_145_out), .cin(adder_171_cout), .cout(adder_145_cout));
  and and_156 (and_156_out, INPUT_1[6], INPUT_2[7]);
  Adder #(.width(1)) adder_146 (
    .a(and_156_out), .b(adder_117_out), .out(adder_146_out), .cin(adder_157_cout), .cout(adder_146_cout));
  and and_157 (and_157_out, INPUT_1[6], INPUT_2[8]);
  Adder #(.width(1)) adder_147 (
    .a(and_157_out), .b(adder_131_out), .out(adder_147_out), .cin(adder_158_cout), .cout(adder_147_cout));
  and and_158 (and_158_out, INPUT_1[6], INPUT_2[9]);
  Adder #(.width(1)) adder_148 (
    .a(and_158_out), .b(adder_132_out), .out(adder_148_out), .cin(adder_159_cout), .cout(adder_148_cout));
  and and_159 (and_159_out, INPUT_1[6], INPUT_2[10]);
  Adder #(.width(1)) adder_149 (
    .a(and_159_out), .b(adder_133_out), .out(adder_149_out), .cin(adder_160_cout), .cout(adder_149_cout));
  and and_160 (and_160_out, INPUT_1[7], INPUT_2[11]);
  and and_161 (and_161_out, INPUT_1[7], INPUT_2[12]);
  Adder #(.width(1)) adder_150 (
    .a(and_161_out), .b(adder_121_out), .out(adder_150_out), .cin(adder_162_cout), .cout(adder_150_cout));
  and and_162 (and_162_out, INPUT_1[7], INPUT_2[13]);
  Adder #(.width(1)) adder_151 (
    .a(and_162_out), .b(adder_136_out), .out(adder_151_out), .cin(adder_163_cout), .cout(adder_151_cout));
  and and_163 (and_163_out, INPUT_1[7], INPUT_2[14]);
  Adder #(.width(1)) adder_152 (
    .a(and_163_out), .b(adder_137_out), .out(adder_152_out), .cin(adder_164_cout), .cout(adder_152_cout));
  and and_164 (and_164_out, INPUT_1[7], INPUT_2[15]);
  Adder #(.width(1)) adder_153 (
    .a(and_164_out), .b(adder_138_out), .out(Z22), .cin(adder_165_cout), .cout(adder_153_cout));
  and and_165 (and_165_out, INPUT_1[4], INPUT_2[0]);
  and and_166 (and_166_out, INPUT_1[3], INPUT_2[1]);
  and and_167 (and_167_out, INPUT_1[3], INPUT_2[2]);
  and and_168 (and_168_out, INPUT_1[4], INPUT_2[3]);
  Adder #(.width(1)) adder_154 (
    .a(and_168_out), .b(adder_127_out), .out(adder_154_out), .cin(adder_168_cout), .cout(adder_154_cout));
  and and_169 (and_169_out, INPUT_1[4], INPUT_2[4]);
  Adder #(.width(1)) adder_155 (
    .a(and_169_out), .b(adder_142_out), .out(adder_155_out), .cin(adder_169_cout), .cout(adder_155_cout));
  and and_170 (and_170_out, INPUT_1[4], INPUT_2[5]);
  Adder #(.width(1)) adder_156 (
    .a(and_170_out), .b(adder_143_out), .out(adder_156_out), .cin(adder_170_cout), .cout(adder_156_cout));
  and and_171 (and_171_out, INPUT_1[4], INPUT_2[6]);
  and and_172 (and_172_out, INPUT_1[5], INPUT_2[7]);
  Adder #(.width(1)) adder_157 (
    .a(and_172_out), .b(adder_130_out), .out(adder_157_out), .cin(adder_172_cout), .cout(adder_157_cout));
  and and_173 (and_173_out, INPUT_1[5], INPUT_2[8]);
  Adder #(.width(1)) adder_158 (
    .a(and_173_out), .b(adder_146_out), .out(adder_158_out), .cin(adder_173_cout), .cout(adder_158_cout));
  and and_174 (and_174_out, INPUT_1[5], INPUT_2[9]);
  Adder #(.width(1)) adder_159 (
    .a(and_174_out), .b(adder_147_out), .out(adder_159_out), .cin(adder_174_cout), .cout(adder_159_cout));
  and and_175 (and_175_out, INPUT_1[5], INPUT_2[10]);
  Adder #(.width(1)) adder_160 (
    .a(and_175_out), .b(adder_148_out), .out(adder_160_out), .cin(adder_175_cout), .cout(adder_160_cout));
  and and_176 (and_176_out, INPUT_1[6], INPUT_2[11]);
  Adder #(.width(1)) adder_161 (
    .a(and_176_out), .b(adder_134_out), .out(adder_161_out), .cin(adder_176_cout), .cout(adder_161_cout));
  and and_177 (and_177_out, INPUT_1[6], INPUT_2[12]);
  Adder #(.width(1)) adder_162 (
    .a(and_177_out), .b(adder_135_out), .out(adder_162_out), .cin(adder_177_cout), .cout(adder_162_cout));
  and and_178 (and_178_out, INPUT_1[6], INPUT_2[13]);
  Adder #(.width(1)) adder_163 (
    .a(and_178_out), .b(adder_150_out), .out(adder_163_out), .cin(adder_178_cout), .cout(adder_163_cout));
  and and_179 (and_179_out, INPUT_1[6], INPUT_2[14]);
  Adder #(.width(1)) adder_164 (
    .a(and_179_out), .b(adder_151_out), .out(adder_164_out), .cin(adder_179_cout), .cout(adder_164_cout));
  and and_180 (and_180_out, INPUT_1[6], INPUT_2[15]);
  Adder #(.width(1)) adder_165 (
    .a(and_180_out), .b(adder_152_out), .out(Z21), .cin(adder_180_cout), .cout(adder_165_cout));
  and and_181 (and_181_out, INPUT_1[3], INPUT_2[0]);
  and and_182 (and_182_out, INPUT_1[2], INPUT_2[1]);
  Adder #(.width(1)) adder_166 (
    .a(and_166_out), .b(and_165_out), .out(adder_166_out), .cin(adder_181_cout), .cout(adder_166_cout));
  and and_183 (and_183_out, INPUT_1[2], INPUT_2[2]);
  Adder #(.width(1)) adder_167 (
    .a(and_167_out), .b(adder_140_out), .out(adder_167_out), .cin(adder_182_cout), .cout(adder_167_cout));
  and and_184 (and_184_out, INPUT_1[3], INPUT_2[3]);
  Adder #(.width(1)) adder_168 (
    .a(and_184_out), .b(adder_141_out), .out(adder_168_out), .cin(adder_183_cout), .cout(adder_168_cout));
  and and_185 (and_185_out, INPUT_1[3], INPUT_2[4]);
  Adder #(.width(1)) adder_169 (
    .a(and_185_out), .b(adder_154_out), .out(adder_169_out), .cin(adder_184_cout), .cout(adder_169_cout));
  and and_186 (and_186_out, INPUT_1[3], INPUT_2[5]);
  Adder #(.width(1)) adder_170 (
    .a(and_186_out), .b(adder_155_out), .out(adder_170_out), .cin(adder_185_cout), .cout(adder_170_cout));
  and and_187 (and_187_out, INPUT_1[3], INPUT_2[6]);
  Adder #(.width(1)) adder_171 (
    .a(and_171_out), .b(adder_144_out), .out(adder_171_out), .cin(adder_186_cout), .cout(adder_171_cout));
  and and_188 (and_188_out, INPUT_1[4], INPUT_2[7]);
  Adder #(.width(1)) adder_172 (
    .a(and_188_out), .b(adder_145_out), .out(adder_172_out), .cin(adder_187_cout), .cout(adder_172_cout));
  and and_189 (and_189_out, INPUT_1[4], INPUT_2[8]);
  Adder #(.width(1)) adder_173 (
    .a(and_189_out), .b(adder_157_out), .out(adder_173_out), .cin(adder_188_cout), .cout(adder_173_cout));
  and and_190 (and_190_out, INPUT_1[4], INPUT_2[9]);
  Adder #(.width(1)) adder_174 (
    .a(and_190_out), .b(adder_158_out), .out(adder_174_out), .cin(adder_189_cout), .cout(adder_174_cout));
  and and_191 (and_191_out, INPUT_1[4], INPUT_2[10]);
  Adder #(.width(1)) adder_175 (
    .a(and_191_out), .b(adder_159_out), .out(adder_175_out), .cin(adder_201_cout), .cout(adder_175_cout));
  and and_192 (and_192_out, INPUT_1[5], INPUT_2[11]);
  Adder #(.width(1)) adder_176 (
    .a(and_192_out), .b(adder_149_out), .out(adder_176_out), .cin(adder_190_cout), .cout(adder_176_cout));
  and and_193 (and_193_out, INPUT_1[5], INPUT_2[12]);
  Adder #(.width(1)) adder_177 (
    .a(and_193_out), .b(adder_161_out), .out(adder_177_out), .cin(adder_191_cout), .cout(adder_177_cout));
  and and_194 (and_194_out, INPUT_1[5], INPUT_2[13]);
  Adder #(.width(1)) adder_178 (
    .a(and_194_out), .b(adder_162_out), .out(adder_178_out), .cin(adder_192_cout), .cout(adder_178_cout));
  and and_195 (and_195_out, INPUT_1[5], INPUT_2[14]);
  Adder #(.width(1)) adder_179 (
    .a(and_195_out), .b(adder_163_out), .out(adder_179_out), .cin(adder_205_cout), .cout(adder_179_cout));
  and and_196 (and_196_out, INPUT_1[5], INPUT_2[15]);
  Adder #(.width(1)) adder_180 (
    .a(and_196_out), .b(adder_164_out), .out(Z20), .cin(adder_206_cout), .cout(adder_180_cout));
  and and_197 (and_197_out, INPUT_1[2], INPUT_2[0]);
  and and_198 (and_198_out, INPUT_1[1], INPUT_2[1]);
  Adder #(.width(1)) adder_181 (
    .a(and_182_out), .b(and_181_out), .out(adder_181_out), .cin(adder_193_cout), .cout(adder_181_cout));
  and and_199 (and_199_out, INPUT_1[1], INPUT_2[2]);
  Adder #(.width(1)) adder_182 (
    .a(and_183_out), .b(adder_166_out), .out(adder_182_out), .cin(adder_194_cout), .cout(adder_182_cout));
  and and_200 (and_200_out, INPUT_1[2], INPUT_2[3]);
  Adder #(.width(1)) adder_183 (
    .a(and_200_out), .b(adder_167_out), .out(adder_183_out), .cin(adder_195_cout), .cout(adder_183_cout));
  and and_201 (and_201_out, INPUT_1[2], INPUT_2[4]);
  Adder #(.width(1)) adder_184 (
    .a(and_201_out), .b(adder_168_out), .out(adder_184_out), .cin(adder_196_cout), .cout(adder_184_cout));
  and and_202 (and_202_out, INPUT_1[2], INPUT_2[5]);
  Adder #(.width(1)) adder_185 (
    .a(and_202_out), .b(adder_169_out), .out(adder_185_out), .cin(adder_211_cout), .cout(adder_185_cout));
  and and_203 (and_203_out, INPUT_1[2], INPUT_2[6]);
  Adder #(.width(1)) adder_186 (
    .a(and_187_out), .b(adder_156_out), .out(adder_186_out), .cin(adder_197_cout), .cout(adder_186_cout));
  and and_204 (and_204_out, INPUT_1[3], INPUT_2[7]);
  Adder #(.width(1)) adder_187 (
    .a(and_204_out), .b(adder_171_out), .out(adder_187_out), .cin(adder_198_cout), .cout(adder_187_cout));
  and and_205 (and_205_out, INPUT_1[3], INPUT_2[8]);
  Adder #(.width(1)) adder_188 (
    .a(and_205_out), .b(adder_172_out), .out(adder_188_out), .cin(adder_199_cout), .cout(adder_188_cout));
  and and_206 (and_206_out, INPUT_1[3], INPUT_2[9]);
  Adder #(.width(1)) adder_189 (
    .a(and_206_out), .b(adder_173_out), .out(adder_189_out), .cin(adder_200_cout), .cout(adder_189_cout));
  and and_207 (and_207_out, INPUT_1[3], INPUT_2[10]);
  and and_208 (and_208_out, INPUT_1[4], INPUT_2[11]);
  Adder #(.width(1)) adder_190 (
    .a(and_208_out), .b(adder_160_out), .out(adder_190_out), .cin(adder_202_cout), .cout(adder_190_cout));
  and and_209 (and_209_out, INPUT_1[4], INPUT_2[12]);
  Adder #(.width(1)) adder_191 (
    .a(and_209_out), .b(adder_176_out), .out(adder_191_out), .cin(adder_203_cout), .cout(adder_191_cout));
  and and_210 (and_210_out, INPUT_1[4], INPUT_2[13]);
  Adder #(.width(1)) adder_192 (
    .a(and_210_out), .b(adder_177_out), .out(adder_192_out), .cin(adder_204_cout), .cout(adder_192_cout));
  and and_211 (and_211_out, INPUT_1[4], INPUT_2[14]);
  and and_212 (and_212_out, INPUT_1[4], INPUT_2[15]);
  and and_213 (and_213_out, INPUT_1[1], INPUT_2[0]);
  and and_214 (and_214_out, INPUT_1[0], INPUT_2[1]);
  Adder #(.width(1)) adder_193 (
    .a(and_198_out), .b(and_197_out), .out(adder_193_out), .cin(adder_207_cout), .cout(adder_193_cout));
  and and_215 (and_215_out, INPUT_1[0], INPUT_2[2]);
  Adder #(.width(1)) adder_194 (
    .a(and_199_out), .b(adder_181_out), .out(adder_194_out), .cin(adder_208_cout), .cout(adder_194_cout));
  and and_216 (and_216_out, INPUT_1[1], INPUT_2[3]);
  Adder #(.width(1)) adder_195 (
    .a(and_216_out), .b(adder_182_out), .out(adder_195_out), .cin(adder_209_cout), .cout(adder_195_cout));
  and and_217 (and_217_out, INPUT_1[1], INPUT_2[4]);
  Adder #(.width(1)) adder_196 (
    .a(and_217_out), .b(adder_183_out), .out(adder_196_out), .cin(adder_210_cout), .cout(adder_196_cout));
  and and_218 (and_218_out, INPUT_1[1], INPUT_2[5]);
  and and_219 (and_219_out, INPUT_1[1], INPUT_2[6]);
  Adder #(.width(1)) adder_197 (
    .a(and_203_out), .b(adder_170_out), .out(adder_197_out), .cin(adder_212_cout), .cout(adder_197_cout));
  and and_220 (and_220_out, INPUT_1[2], INPUT_2[7]);
  Adder #(.width(1)) adder_198 (
    .a(and_220_out), .b(adder_186_out), .out(adder_198_out), .cin(adder_213_cout), .cout(adder_198_cout));
  and and_221 (and_221_out, INPUT_1[2], INPUT_2[8]);
  Adder #(.width(1)) adder_199 (
    .a(and_221_out), .b(adder_187_out), .out(adder_199_out), .cin(adder_214_cout), .cout(adder_199_cout));
  and and_222 (and_222_out, INPUT_1[2], INPUT_2[9]);
  Adder #(.width(1)) adder_200 (
    .a(and_222_out), .b(adder_188_out), .out(adder_200_out), .cin(adder_223_cout), .cout(adder_200_cout));
  and and_223 (and_223_out, INPUT_1[2], INPUT_2[10]);
  Adder #(.width(1)) adder_201 (
    .a(and_207_out), .b(adder_174_out), .out(adder_201_out), .cin(adder_215_cout), .cout(adder_201_cout));
  and and_224 (and_224_out, INPUT_1[3], INPUT_2[11]);
  Adder #(.width(1)) adder_202 (
    .a(and_224_out), .b(adder_175_out), .out(adder_202_out), .cin(adder_216_cout), .cout(adder_202_cout));
  and and_225 (and_225_out, INPUT_1[3], INPUT_2[12]);
  Adder #(.width(1)) adder_203 (
    .a(and_225_out), .b(adder_190_out), .out(adder_203_out), .cin(adder_217_cout), .cout(adder_203_cout));
  and and_226 (and_226_out, INPUT_1[3], INPUT_2[13]);
  Adder #(.width(1)) adder_204 (
    .a(and_226_out), .b(adder_191_out), .out(adder_204_out), .cin(adder_226_cout), .cout(adder_204_cout));
  and and_227 (and_227_out, INPUT_1[3], INPUT_2[14]);
  Adder #(.width(1)) adder_205 (
    .a(and_211_out), .b(adder_178_out), .out(adder_205_out), .cin(adder_218_cout), .cout(adder_205_cout));
  and and_228 (and_228_out, INPUT_1[3], INPUT_2[15]);
  Adder #(.width(1)) adder_206 (
    .a(and_212_out), .b(adder_179_out), .out(Z19), .cin(adder_219_cout), .cout(adder_206_cout));
  and and_229 (out_3[0], INPUT_1[0], INPUT_2[0]);
  Adder #(.width(1)) adder_207 (.a(and_214_out), .b(and_213_out), .out(out_3[1]), .cout(adder_207_cout));  // open: cin
  Adder #(.width(1)) adder_208 (
    .a(and_215_out), .b(adder_193_out), .out(out_3[2]), .cout(adder_208_cout));  // open: cin
  and and_230 (and_230_out, INPUT_1[0], INPUT_2[3]);
  Adder #(.width(1)) adder_209 (
    .a(and_230_out), .b(adder_194_out), .out(out_3[3]), .cout(adder_209_cout));  // open: cin
  and and_231 (and_231_out, INPUT_1[0], INPUT_2[4]);
  Adder #(.width(1)) adder_210 (
    .a(and_231_out), .b(adder_195_out), .out(out_3[4]), .cout(adder_210_cout));  // open: cin
  and and_232 (and_232_out, INPUT_1[0], INPUT_2[5]);
  Adder #(.width(1)) adder_211 (
    .a(and_218_out), .b(adder_184_out), .out(adder_211_out), .cin(adder_220_cout), .cout(adder_211_cout));
  and and_233 (and_233_out, INPUT_1[0], INPUT_2[6]);
  Adder #(.width(1)) adder_212 (
    .a(and_219_out), .b(adder_185_out), .out(adder_212_out), .cin(adder_221_cout), .cout(adder_212_cout));
  and and_234 (and_234_out, INPUT_1[1], INPUT_2[7]);
  Adder #(.width(1)) adder_213 (
    .a(and_234_out), .b(adder_197_out), .out(adder_213_out), .cin(adder_222_cout), .cout(adder_213_cout));
  and and_235 (and_235_out, INPUT_1[1], INPUT_2[8]);
  Adder #(.width(1)) adder_214 (
    .a(and_235_out), .b(adder_198_out), .out(adder_214_out), .cin(adder_229_cout), .cout(adder_214_cout));
  and and_236 (and_236_out, INPUT_1[1], INPUT_2[9]);
  and and_237 (and_237_out, INPUT_1[1], INPUT_2[10]);
  Adder #(.width(1)) adder_215 (
    .a(and_223_out), .b(adder_189_out), .out(adder_215_out), .cin(adder_224_cout), .cout(adder_215_cout));
  and and_238 (and_238_out, INPUT_1[2], INPUT_2[11]);
  Adder #(.width(1)) adder_216 (
    .a(and_238_out), .b(adder_201_out), .out(adder_216_out), .cin(adder_225_cout), .cout(adder_216_cout));
  and and_239 (and_239_out, INPUT_1[2], INPUT_2[12]);
  Adder #(.width(1)) adder_217 (
    .a(and_239_out), .b(adder_202_out), .out(adder_217_out), .cin(adder_233_cout), .cout(adder_217_cout));
  and and_240 (and_240_out, INPUT_1[2], INPUT_2[13]);
  and and_241 (and_241_out, INPUT_1[2], INPUT_2[14]);
  Adder #(.width(1)) adder_218 (
    .a(and_227_out), .b(adder_192_out), .out(adder_218_out), .cin(adder_227_cout), .cout(adder_218_cout));
  and and_242 (and_242_out, INPUT_1[2], INPUT_2[15]);
  Adder #(.width(1)) adder_219 (
    .a(and_228_out), .b(adder_205_out), .out(Z18), .cin(adder_228_cout), .cout(adder_219_cout));
  Adder #(.width(1)) adder_220 (
    .a(and_232_out), .b(adder_196_out), .out(out_3[5]), .cout(adder_220_cout));  // open: cin
  Adder #(.width(1)) adder_221 (
    .a(and_233_out), .b(adder_211_out), .out(out_3[6]), .cout(adder_221_cout));  // open: cin
  and and_243 (and_243_out, INPUT_1[0], INPUT_2[7]);
  Adder #(.width(1)) adder_222 (
    .a(and_243_out), .b(adder_212_out), .out(out_3[7]), .cout(adder_222_cout));  // open: cin
  and and_244 (and_244_out, INPUT_1[0], INPUT_2[8]);
  and and_245 (and_245_out, INPUT_1[0], INPUT_2[9]);
  Adder #(.width(1)) adder_223 (
    .a(and_236_out), .b(adder_199_out), .out(adder_223_out), .cin(adder_230_cout), .cout(adder_223_cout));
  and and_246 (and_246_out, INPUT_1[0], INPUT_2[10]);
  Adder #(.width(1)) adder_224 (
    .a(and_237_out), .b(adder_200_out), .out(adder_224_out), .cin(adder_231_cout), .cout(adder_224_cout));
  and and_247 (and_247_out, INPUT_1[1], INPUT_2[11]);
  Adder #(.width(1)) adder_225 (
    .a(and_247_out), .b(adder_215_out), .out(adder_225_out), .cin(adder_232_cout), .cout(adder_225_cout));
  and and_248 (and_248_out, INPUT_1[1], INPUT_2[12]);
  and and_249 (and_249_out, INPUT_1[1], INPUT_2[13]);
  Adder #(.width(1)) adder_226 (
    .a(and_240_out), .b(adder_203_out), .out(adder_226_out), .cin(adder_234_cout), .cout(adder_226_cout));
  and and_250 (and_250_out, INPUT_1[1], INPUT_2[14]);
  Adder #(.width(1)) adder_227 (
    .a(and_241_out), .b(adder_204_out), .out(adder_227_out), .cin(adder_235_cout), .cout(adder_227_cout));
  and and_251 (and_251_out, INPUT_1[1], INPUT_2[15]);
  Adder #(.width(1)) adder_228 (
    .a(and_242_out), .b(adder_218_out), .out(Z17), .cin(adder_236_cout), .cout(adder_228_cout));
  Adder #(.width(1)) adder_229 (
    .a(and_244_out), .b(adder_213_out), .out(out_3[8]), .cout(adder_229_cout));  // open: cin
  Adder #(.width(1)) adder_230 (
    .a(and_245_out), .b(adder_214_out), .out(out_3[9]), .cout(adder_230_cout));  // open: cin
  Adder #(.width(1)) adder_231 (
    .a(and_246_out), .b(adder_223_out), .out(out_3[10]), .cout(adder_231_cout));  // open: cin
  and and_252 (and_252_out, INPUT_1[0], INPUT_2[11]);
  Adder #(.width(1)) adder_232 (.a(and_252_out), .b(adder_224_out), .out(Z11), .cout(adder_232_cout));  // open: cin
  and and_253 (and_253_out, INPUT_1[0], INPUT_2[12]);
  Adder #(.width(1)) adder_233 (
    .a(and_248_out), .b(adder_216_out), .out(adder_233_out), .cin(adder_237_cout), .cout(adder_233_cout));
  and and_254 (and_254_out, INPUT_1[0], INPUT_2[13]);
  Adder #(.width(1)) adder_234 (
    .a(and_249_out), .b(adder_217_out), .out(adder_234_out), .cin(adder_238_cout), .cout(adder_234_cout));
  and and_255 (and_255_out, INPUT_1[0], INPUT_2[14]);
  Adder #(.width(1)) adder_235 (
    .a(and_250_out), .b(adder_226_out), .out(adder_235_out), .cin(adder_239_cout), .cout(adder_235_cout));
  and and_256 (and_256_out, INPUT_1[0], INPUT_2[15]);
  Adder #(.width(1)) adder_236 (
    .a(and_251_out), .b(adder_227_out), .out(Z16), .cin(adder_240_cout), .cout(adder_236_cout));
  Adder #(.width(1)) adder_237 (.a(and_253_out), .b(adder_225_out), .out(Z12), .cout(adder_237_cout));  // open: cin
  Adder #(.width(1)) adder_238 (.a(and_254_out), .b(adder_233_out), .out(Z13), .cout(adder_238_cout));  // open: cin
  Adder #(.width(1)) adder_239 (.a(and_255_out), .b(adder_234_out), .out(Z14), .cout(adder_239_cout));  // open: cin
  Adder #(.width(1)) adder_240 (.a(and_256_out), .b(adder_235_out), .out(Z15), .cout(adder_240_cout));  // open: cin

  // Notes on the sheet:
  //   16 x 16  Multiplier
  //   Niloy Biswas
  //   ID - 1520022042
endmodule

module Booth_s_Algorithm (
  input  [4:0] M,
  input  [4:0] A,
  output q9,
  output q8,
  output q7,
  output q6,
  output q5,
  output q4,
  output q3,
  output q2,
  output out_11,
  output q1,
  output q0,
  output q_1
);

  wire adder_1_cout, adder_1_out, adder_2_cout, adder_2_out, adder_3_cout, adder_3_out, adder_4_cout,
       adder_4_out, adder_5_out, and_1_out, and_2_out, and_3_out, and_4_out, and_5_out, and_6_out, and_7_out,
       and_8_out, and_9_out, and_10_out, and_11_out, and_12_out, d_ff_1_q, d_ff_1_qn, or_1_out, or_2_out,
       or_3_out, or_4_out, or_5_out, or_6_out, xor_1_out, xor_2_out, xor_3_out, xor_4_out, xor_5_out,
       xor_6_out;

  and and_1 (and_1_out, A[0], d_ff_1_qn);
  and and_2 (and_2_out, M[0], xor_6_out);
  and and_3 (and_3_out, M[1], xor_6_out);
  and and_4 (and_4_out, M[2], xor_6_out);
  and and_5 (and_5_out, M[3], xor_6_out);
  and and_6 (and_6_out, M[4], xor_6_out);
  or or_1 (or_1_out, and_1_out, q0);
  xor xor_1 (xor_1_out, and_2_out, and_7_out);
  xor xor_2 (xor_2_out, and_3_out, and_7_out);
  xor xor_3 (xor_3_out, and_4_out, and_7_out);
  xor xor_4 (xor_4_out, and_5_out, and_7_out);
  xor xor_5 (xor_5_out, and_6_out, and_7_out);
  xor xor_6 (xor_6_out, or_1_out, q_1);
  and and_7 (and_7_out, xor_6_out, or_1_out);
  Adder #(.width(1)) adder_1 (.a(q5), .b(xor_1_out), .out(adder_1_out), .cin(and_7_out), .cout(adder_1_cout));
  Adder #(.width(1)) adder_2 (.a(q6), .b(xor_2_out), .out(adder_2_out), .cin(adder_1_cout), .cout(adder_2_cout));
  Adder #(.width(1)) adder_3 (.a(q7), .b(xor_3_out), .out(adder_3_out), .cin(adder_2_cout), .cout(adder_3_cout));
  Adder #(.width(1)) adder_4 (.a(q8), .b(xor_4_out), .out(adder_4_out), .cin(adder_3_cout), .cout(adder_4_cout));
  Adder #(.width(1)) adder_5 (.a(q9), .b(xor_5_out), .out(adder_5_out), .cin(adder_4_cout), .cout(out_11));
  D_Flip_Flop d_ff_1 (.D(1'b1), .Q(d_ff_1_q), .Qn(d_ff_1_qn));  // open: clk, preset, en, reset
  and and_8 (and_8_out, d_ff_1_qn, A[4]);
  and and_9 (and_9_out, d_ff_1_qn, A[3]);
  and and_10 (and_10_out, d_ff_1_qn, A[2]);
  and and_11 (and_11_out, d_ff_1_qn, A[1]);
  and and_12 (and_12_out, d_ff_1_qn, A[0]);
  or or_2 (or_2_out, and_8_out, adder_1_out);
  or or_3 (or_3_out, and_9_out, q4);
  or or_4 (or_4_out, and_10_out, q3);
  or or_5 (or_5_out, and_11_out, q2);
  or or_6 (or_6_out, and_12_out, q1);
  Register #(.width(1)) register_1 (.D(adder_5_out), .Q(q9));  // open: en, clk, clr
  Register #(.width(1)) register_2 (.D(adder_5_out), .Q(q8));  // open: en, clk, clr
  Register #(.width(1)) register_3 (.D(adder_4_out), .Q(q7));  // open: en, clk, clr
  Register #(.width(1)) register_4 (.D(adder_3_out), .Q(q6));  // open: en, clk, clr
  Register #(.width(1)) register_5 (.D(adder_2_out), .Q(q5));  // open: en, clk, clr
  Register #(.width(1)) register_6 (.D(or_2_out), .Q(q4));  // open: en, clk, clr
  Register #(.width(1)) register_7 (.D(or_3_out), .Q(q3));  // open: en, clk, clr
  Register #(.width(1)) register_8 (.D(or_4_out), .Q(q2));  // open: en, clk, clr
  Register #(.width(1)) register_9 (.D(or_5_out), .Q(q1));  // open: en, clk, clr
  Register #(.width(1)) register_10 (.D(or_6_out), .Q(q0));  // open: en, clk, clr
  Register #(.width(1)) register_11 (.D(q0), .Q(q_1));  // open: en, clk, clr

  // Notes on the sheet:
  //   Booth's Algorithm
  //   Niloy Biswas
  //   ID - 1520022042
  //   (Attempt)
  //   A0
  //   Q'
endmodule

module Register_File (
  input  Clock,
  input  [15:0] Data_IN,
  input  RegWrite,
  input  [3:0] RS,
  input  [3:0] RD,
  input  [3:0] RT,
  output [15:0] Data01,
  output [15:0] Data02
);

  wire and_1_out, and_2_out, and_3_out, and_4_out, and_5_out, and_6_out, and_7_out, and_8_out, and_9_out,
       and_10_out, and_11_out, and_12_out, and_13_out, and_14_out, and_15_out, and_16_out, decoder_1_out0,
       decoder_1_out1, decoder_1_out2, decoder_1_out3, decoder_1_out4, decoder_1_out5, decoder_1_out6,
       decoder_1_out7, decoder_1_out8, decoder_1_out9, decoder_1_out10, decoder_1_out11, decoder_1_out12,
       decoder_1_out13, decoder_1_out14, decoder_1_out15;
  wire [15:0] register_1_q, register_2_q, register_3_q, register_4_q, register_5_q, register_6_q,
       register_7_q, register_8_q, register_9_q, register_10_q, register_11_q, register_12_q, register_13_q,
       register_14_q, register_15_q, register_16_q;

  Decoder #(.select(4)) decoder_1 (
    .out0(decoder_1_out0), .out1(decoder_1_out1), .out2(decoder_1_out2), .out3(decoder_1_out3),
    .out4(decoder_1_out4), .out5(decoder_1_out5), .out6(decoder_1_out6), .out7(decoder_1_out7),
    .out8(decoder_1_out8), .out9(decoder_1_out9), .out10(decoder_1_out10), .out11(decoder_1_out11),
    .out12(decoder_1_out12), .out13(decoder_1_out13), .out14(decoder_1_out14), .out15(decoder_1_out15),
    .sel(RD));  // open: en
  and and_1 (and_1_out, RegWrite, decoder_1_out0);
  and and_2 (and_2_out, RegWrite, decoder_1_out1);
  and and_3 (and_3_out, RegWrite, decoder_1_out2);
  and and_4 (and_4_out, RegWrite, decoder_1_out3);
  and and_5 (and_5_out, RegWrite, decoder_1_out4);
  and and_6 (and_6_out, RegWrite, decoder_1_out5);
  and and_7 (and_7_out, RegWrite, decoder_1_out6);
  and and_8 (and_8_out, RegWrite, decoder_1_out7);
  and and_9 (and_9_out, RegWrite, decoder_1_out8);
  and and_10 (and_10_out, RegWrite, decoder_1_out9);
  and and_11 (and_11_out, RegWrite, decoder_1_out10);
  and and_12 (and_12_out, RegWrite, decoder_1_out11);
  and and_13 (and_13_out, RegWrite, decoder_1_out12);
  and and_14 (and_14_out, RegWrite, decoder_1_out13);
  and and_15 (and_15_out, RegWrite, decoder_1_out14);
  and and_16 (and_16_out, RegWrite, decoder_1_out15);
  Register #(.width(16)) register_1 (.D(Data_IN), .en(and_1_out), .Q(register_1_q), .clk(Clock));  // open: clr
  Register #(.width(16)) register_2 (.D(Data_IN), .en(and_2_out), .Q(register_2_q), .clk(Clock));  // open: clr
  Register #(.width(16)) register_3 (.D(Data_IN), .en(and_3_out), .Q(register_3_q), .clk(Clock));  // open: clr
  Register #(.width(16)) register_4 (.D(Data_IN), .en(and_4_out), .Q(register_4_q), .clk(Clock));  // open: clr
  Register #(.width(16)) register_5 (.D(Data_IN), .en(and_5_out), .Q(register_5_q), .clk(Clock));  // open: clr
  Register #(.width(16)) register_6 (.D(Data_IN), .en(and_6_out), .Q(register_6_q), .clk(Clock));  // open: clr
  Register #(.width(16)) register_7 (.D(Data_IN), .en(and_7_out), .Q(register_7_q), .clk(Clock));  // open: clr
  Register #(.width(16)) register_8 (.D(Data_IN), .en(and_8_out), .Q(register_8_q), .clk(Clock));  // open: clr
  Register #(.width(16)) register_9 (.D(Data_IN), .en(and_9_out), .Q(register_9_q), .clk(Clock));  // open: clr
  Register #(.width(16)) register_10 (.D(Data_IN), .en(and_10_out), .Q(register_10_q), .clk(Clock));  // open: clr
  Register #(.width(16)) register_11 (.D(Data_IN), .en(and_11_out), .Q(register_11_q), .clk(Clock));  // open: clr
  Register #(.width(16)) register_12 (.D(Data_IN), .en(and_12_out), .Q(register_12_q), .clk(Clock));  // open: clr
  Register #(.width(16)) register_13 (.D(Data_IN), .en(and_13_out), .Q(register_13_q), .clk(Clock));  // open: clr
  Register #(.width(16)) register_14 (.D(Data_IN), .en(and_14_out), .Q(register_14_q), .clk(Clock));  // open: clr
  Register #(.width(16)) register_15 (.D(Data_IN), .en(and_15_out), .Q(register_15_q), .clk(Clock));  // open: clr
  Register #(.width(16)) register_16 (.D(Data_IN), .en(and_16_out), .Q(register_16_q), .clk(Clock));  // open: clr
  Multiplexer #(.select(4), .width(16)) multiplexer_1 (
    .in0(register_1_q), .in1(register_2_q), .in2(register_3_q), .in3(register_4_q), .in4(register_5_q),
    .in5(register_6_q), .in6(register_7_q), .in7(register_8_q), .in8(register_9_q), .in9(register_10_q),
    .in10(register_11_q), .in11(register_12_q), .in12(register_13_q), .in13(register_14_q),
    .in14(register_15_q), .in15(register_16_q), .out(Data01), .sel(RS));  // open: en
  Multiplexer #(.select(4), .width(16)) multiplexer_2 (
    .in0(register_1_q), .in1(register_2_q), .in2(register_3_q), .in3(register_4_q), .in4(register_5_q),
    .in5(register_6_q), .in6(register_7_q), .in7(register_8_q), .in8(register_9_q), .in9(register_10_q),
    .in10(register_11_q), .in11(register_12_q), .in12(register_13_q), .in13(register_14_q),
    .in14(register_15_q), .in15(register_16_q), .out(Data02), .sel(RT));  // open: en

  // Notes on the sheet:
  //   ASIF MAHMUD
  //   ID- 1511190642
  //   Register Files
endmodule

module Experimental (
  input  in_1,
  input  [15:0] in_2,
  input  [15:0] in_3,
  input  [3:0] in_4,
  input  [3:0] in_5,
  input  [3:0] in_6,
  input  [15:0] in_7,
  input  in_8,
  input  [15:0] in_9,
  input  [3:0] in_10,
  input  [3:0] in_11,
  input  [15:0] in_12,
  input  [3:0] in_13,
  output [15:0] out_14,
  output [15:0] out_15,
  output [15:0] out_16,
  output [15:0] out_17,
  output [15:0] out_18,
  output [15:0] out_19,
  output [15:0] out_20
);

  wire button_1_out;

  Button button_1 (.out(button_1_out));
  Sign_Extention_16_bits sign_extention_16_bits_1 (.in_1(in_11), .out_2(out_19));
  // Register_File register_file_1: pin names not known; wires that end beside it: in_4, in_5, in_6, in_7, button_1_out, in_8, out_17
  _16_Bit_CLA u_16_bit_cla_1 (.Cin(in_1), .in_2(in_2), .in_3(in_3), .Out_put(out_14));  // open: Cout
  Adder #(.width(16)) adder_1 (.a(in_2), .b(in_3), .out(out_15));  // open: cin, cout
  SRL srl_1 (.in_1(in_10), .in_2(in_9), .out_3(out_18));
  SLL sll_1 (.in_1(in_12), .in_2(in_13), .out_3(out_20));

  assign out_16 = out_15;
endmodule

module ALU (
  input  Cin,
  input  [15:0] Data_1,
  input  [15:0] Data_2,
  input  A_invert,
  input  B_invert,
  input  [3:0] Shift_Ammount,
  input  [2:0] ALU_Op,
  output Zero_Flag,
  output [15:0] Result
);

  wire [15:0] and_1_out, multiplexer_1_out, multiplexer_2_out, multiplier_1_out, n16_bit_cla_1_out_put,
       not_1_out, not_2_out, or_1_out, sll_1_out_3, srl_1_out_3, xor_1_out;

  assign not_1_out = ~Data_1;  // NOT_Gate not_1, 16 bits wide
  assign not_2_out = ~Data_2;  // NOT_Gate not_2, 16 bits wide
  Multiplexer #(.width(16)) multiplexer_1 (
    .in0(Data_1), .in1(not_1_out), .out(multiplexer_1_out), .sel(A_invert));  // open: en
  Multiplexer #(.width(16)) multiplexer_2 (
    .in0(Data_2), .in1(not_2_out), .out(multiplexer_2_out), .sel(B_invert));  // open: en
  _16_Bit_CLA u_16_bit_cla_1 (
    .Cin(Cin), .in_2(multiplexer_1_out), .in_3(multiplexer_2_out), .Out_put(n16_bit_cla_1_out_put));  // open: Cout
  assign and_1_out = multiplexer_1_out & multiplexer_2_out;  // AND_Gate and_1, 16 bits wide
  assign or_1_out = multiplexer_1_out | multiplexer_2_out;  // OR_Gate or_1, 16 bits wide
  assign xor_1_out = multiplexer_1_out ^ multiplexer_2_out;  // XOR_Gate xor_1, 16 bits wide
  SLL sll_1 (.in_1(multiplexer_1_out), .in_2(Shift_Ammount), .out_3(sll_1_out_3));
  SRL srl_1 (.in_1(Shift_Ammount), .in_2(multiplexer_1_out), .out_3(srl_1_out_3));
  Multiplier #(.width(16)) multiplier_1 (
    .a(multiplexer_1_out), .b(multiplexer_2_out), .out(multiplier_1_out));  // open: cin, cout
  Multiplexer #(.select(3), .width(16)) multiplexer_3 (
    .in0(n16_bit_cla_1_out_put), .in1(and_1_out), .in2(or_1_out), .in3(xor_1_out), .in4(sll_1_out_3),
    .in5(srl_1_out_3), .in6(multiplier_1_out), .out(Result), .sel(ALU_Op));  // open: in7, en
  nor nor_1 (Zero_Flag, Result[0], Result[1], Result[2], Result[3], Result[4], Result[5], Result[6], Result[7], Result[8], Result[9], Result[10], Result[11], Result[12], Result[13], Result[14], Result[15]);

  // Notes on the sheet:
  //   ASIF MAHMUD
  //   ID- 1511190642
endmodule

module Control (
  input  [3:0] Op_Code,
  output A_Invert,
  output B_Invert,
  output REG_Write,
  output ALUSrc,
  output REGdst,
  output MemToReg,
  output MemRead,
  output MemWrite,
  output Branch,
  output [2:0] ALU_OP,
  output Shift,
  output Jump
);

  wire and_1_out, and_2_out, and_3_out, and_4_out, and_5_out, and_6_out, and_7_out, and_8_out, and_9_out,
       and_11_out, and_12_out, and_13_out, and_17_out, and_18_out, and_19_out, and_20_out, and_21_out,
       and_22_out, and_23_out, and_24_out, and_25_out, and_26_out, not_1_out, not_2_out, not_3_out,
       not_4_out, not_5_out, not_6_out, not_7_out, not_8_out, not_9_out, not_10_out, not_11_out, not_12_out,
       not_13_out, not_14_out, not_15_out, not_16_out, not_17_out, not_18_out, not_19_out, not_20_out,
       not_21_out, not_22_out, not_23_out, not_24_out, not_25_out, not_26_out, not_27_out, not_28_out,
       not_29_out, not_30_out, not_31_out, not_32_out, not_33_out, not_34_out, not_35_out, not_36_out,
       not_37_out, not_38_out;

  not not_1 (not_1_out, Op_Code[3]);
  not not_2 (not_2_out, Op_Code[2]);
  not not_3 (not_3_out, Op_Code[3]);
  not not_4 (not_4_out, Op_Code[2]);
  not not_5 (not_5_out, Op_Code[0]);
  not not_6 (not_6_out, Op_Code[2]);
  not not_7 (not_7_out, Op_Code[1]);
  not not_8 (not_8_out, Op_Code[0]);
  not not_9 (not_9_out, Op_Code[0]);
  not not_10 (not_10_out, Op_Code[2]);
  not not_11 (not_11_out, Op_Code[0]);
  not not_12 (not_12_out, Op_Code[3]);
  not not_13 (not_13_out, Op_Code[2]);
  not not_14 (not_14_out, Op_Code[0]);
  not not_15 (not_15_out, Op_Code[3]);
  not not_16 (not_16_out, Op_Code[2]);
  not not_17 (not_17_out, Op_Code[1]);
  not not_18 (not_18_out, Op_Code[3]);
  not not_19 (not_19_out, Op_Code[2]);
  not not_20 (not_20_out, Op_Code[0]);
  not not_21 (not_21_out, Op_Code[1]);
  and and_1 (and_1_out, not_1_out, not_2_out);
  and and_2 (and_2_out, not_3_out, Op_Code[0]);
  and and_3 (and_3_out, not_4_out, Op_Code[0]);
  and and_4 (and_4_out, Op_Code[3], Op_Code[2], not_5_out);
  and and_5 (and_5_out, Op_Code[3], not_6_out);
  and and_6 (and_6_out, Op_Code[3], not_7_out);
  and and_7 (and_7_out, Op_Code[3], not_8_out);
  and and_8 (and_8_out, Op_Code[3], Op_Code[1], not_9_out);
  and and_9 (and_9_out, Op_Code[3], Op_Code[2], Op_Code[1]);
  not not_22 (not_22_out, Op_Code[2]);
  not not_23 (not_23_out, Op_Code[1]);
  not not_24 (not_24_out, Op_Code[2]);
  not not_25 (not_25_out, Op_Code[0]);
  not not_26 (not_26_out, Op_Code[3]);
  not not_27 (not_27_out, Op_Code[1]);
  not not_28 (not_28_out, Op_Code[0]);
  not not_29 (not_29_out, Op_Code[2]);
  not not_30 (not_30_out, Op_Code[3]);
  not not_31 (not_31_out, Op_Code[3]);
  not not_32 (not_32_out, Op_Code[1]);
  not not_33 (not_33_out, Op_Code[0]);
  not not_34 (not_34_out, Op_Code[3]);
  not not_35 (not_35_out, Op_Code[1]);
  not not_36 (not_36_out, Op_Code[0]);
  not not_37 (not_37_out, Op_Code[3]);
  not not_38 (not_38_out, Op_Code[0]);
  and and_10 (A_Invert, not_12_out, not_13_out, Op_Code[1], not_14_out);
  and and_11 (and_11_out, not_15_out, not_16_out, not_17_out, Op_Code[0]);
  and and_12 (and_12_out, not_18_out, not_19_out, Op_Code[1], not_20_out);
  and and_13 (and_13_out, Op_Code[3], Op_Code[2], Op_Code[1], Op_Code[0]);
  or or_1 (ALUSrc, and_5_out, and_6_out, and_7_out);
  or or_2 (REGdst, and_8_out, and_9_out);
  and and_14 (MemRead, Op_Code[3], not_22_out, not_23_out, Op_Code[0]);
  and and_15 (MemWrite, Op_Code[3], not_24_out, Op_Code[1], not_25_out);
  and and_16 (Branch, Op_Code[3], Op_Code[2], Op_Code[1], Op_Code[0]);
  and and_17 (and_17_out, not_26_out, Op_Code[2], Op_Code[1], Op_Code[0]);
  and and_18 (and_18_out, Op_Code[3], Op_Code[2], not_27_out, Op_Code[0]);
  and and_19 (and_19_out, Op_Code[3], Op_Code[2], Op_Code[1], not_28_out);
  and and_20 (and_20_out, not_29_out, Op_Code[1], Op_Code[0]);
  and and_21 (and_21_out, not_30_out, Op_Code[2], Op_Code[0]);
  and and_22 (and_22_out, not_31_out, Op_Code[2], not_32_out);
  and and_23 (and_23_out, Op_Code[3], Op_Code[2], not_33_out);
  and and_24 (and_24_out, not_34_out, not_10_out, Op_Code[1], not_11_out);
  and and_25 (and_25_out, Op_Code[3], Op_Code[2], not_35_out, Op_Code[0]);
  and and_26 (and_26_out, Op_Code[3], Op_Code[2], Op_Code[1], not_36_out);
  and and_27 (Jump, not_37_out, Op_Code[2], Op_Code[1], not_38_out);
  or or_3 (B_Invert, and_11_out, and_12_out, and_13_out);
  or or_4 (REG_Write, not_21_out, and_1_out, and_2_out, and_3_out, and_4_out);
  or or_5 (ALU_OP[0], and_22_out, and_23_out, and_24_out);
  or or_6 (Shift, and_25_out, and_26_out);
  or or_7 (ALU_OP[2], and_17_out, and_18_out, and_19_out);
  or or_8 (ALU_OP[1], and_20_out, and_21_out);

  assign MemToReg = MemRead;

  // Notes on the sheet:
  //   ASIF MAHMUD
  //   ID- 1511190642
endmodule

module SRL (
  input  [3:0] in_1,
  input  [15:0] in_2,
  output [15:0] out_3
);

  Multiplexer #(.select(4)) multiplexer_1 (
    .in0(in_2[0]), .in1(in_2[1]), .in2(in_2[2]), .in3(in_2[3]), .in4(in_2[4]), .in5(in_2[5]), .in6(in_2[6]),
    .in7(in_2[7]), .in8(in_2[8]), .in9(in_2[9]), .in10(in_2[10]), .in11(in_2[11]), .in12(in_2[12]),
    .in13(in_2[13]), .in14(in_2[14]), .in15(in_2[15]), .out(out_3[0]), .sel(in_1));  // open: en
  Multiplexer #(.select(4)) multiplexer_2 (
    .in0(in_2[1]), .in1(in_2[2]), .in2(in_2[3]), .in3(in_2[4]), .in4(in_2[5]), .in5(in_2[6]), .in6(in_2[7]),
    .in7(in_2[8]), .in8(in_2[9]), .in9(in_2[10]), .in10(in_2[11]), .in11(in_2[12]), .in12(in_2[13]),
    .in13(in_2[14]), .in14(in_2[15]), .in15(1'b0), .out(out_3[1]), .sel(in_1));  // open: en
  Multiplexer #(.select(4)) multiplexer_3 (
    .in0(in_2[2]), .in1(in_2[3]), .in2(in_2[4]), .in3(in_2[5]), .in4(in_2[6]), .in5(in_2[7]), .in6(in_2[8]),
    .in7(in_2[9]), .in8(in_2[10]), .in9(in_2[11]), .in10(in_2[12]), .in11(in_2[13]), .in12(in_2[14]),
    .in13(in_2[15]), .in14(1'b0), .in15(1'b0), .out(out_3[2]), .sel(in_1));  // open: en
  Multiplexer #(.select(4)) multiplexer_4 (
    .in0(in_2[3]), .in1(in_2[4]), .in2(in_2[5]), .in3(in_2[6]), .in4(in_2[7]), .in5(in_2[8]), .in6(in_2[9]),
    .in7(in_2[10]), .in8(in_2[11]), .in9(in_2[12]), .in10(in_2[13]), .in11(in_2[14]), .in12(in_2[15]),
    .in13(1'b0), .in14(1'b0), .in15(1'b0), .out(out_3[3]), .sel(in_1));  // open: en
  Multiplexer #(.select(4)) multiplexer_5 (
    .in0(in_2[4]), .in1(in_2[5]), .in2(in_2[6]), .in3(in_2[7]), .in4(in_2[8]), .in5(in_2[9]), .in6(in_2[10]),
    .in7(in_2[11]), .in8(in_2[12]), .in9(in_2[13]), .in10(in_2[14]), .in11(in_2[15]), .in12(1'b0),
    .in13(1'b0), .in14(1'b0), .in15(1'b0), .out(out_3[4]), .sel(in_1));  // open: en
  Multiplexer #(.select(4)) multiplexer_6 (
    .in0(in_2[5]), .in1(in_2[6]), .in2(in_2[7]), .in3(in_2[8]), .in4(in_2[9]), .in5(in_2[10]),
    .in6(in_2[11]), .in7(in_2[12]), .in8(in_2[13]), .in9(in_2[14]), .in10(in_2[15]), .in11(1'b0),
    .in12(1'b0), .in13(1'b0), .in14(1'b0), .in15(1'b0), .out(out_3[5]), .sel(in_1));  // open: en
  Multiplexer #(.select(4)) multiplexer_7 (
    .in0(in_2[6]), .in1(in_2[7]), .in2(in_2[8]), .in3(in_2[9]), .in4(in_2[10]), .in5(in_2[11]),
    .in6(in_2[12]), .in7(in_2[13]), .in8(in_2[14]), .in9(in_2[15]), .in10(1'b0), .in11(1'b0), .in12(1'b0),
    .in13(1'b0), .in14(1'b0), .in15(1'b0), .out(out_3[6]), .sel(in_1));  // open: en
  Multiplexer #(.select(4)) multiplexer_8 (
    .in0(in_2[7]), .in1(in_2[8]), .in2(in_2[9]), .in3(in_2[10]), .in4(in_2[11]), .in5(in_2[12]),
    .in6(in_2[13]), .in7(in_2[14]), .in8(in_2[15]), .in9(1'b0), .in10(1'b0), .in11(1'b0), .in12(1'b0),
    .in13(1'b0), .in14(1'b0), .in15(1'b0), .out(out_3[7]), .sel(in_1));  // open: en
  Multiplexer #(.select(4)) multiplexer_9 (
    .in0(in_2[8]), .in1(in_2[9]), .in2(in_2[10]), .in3(in_2[11]), .in4(in_2[12]), .in5(in_2[13]),
    .in6(in_2[14]), .in7(in_2[15]), .in8(1'b0), .in9(1'b0), .in10(1'b0), .in11(1'b0), .in12(1'b0),
    .in13(1'b0), .in14(1'b0), .in15(1'b0), .out(out_3[8]), .sel(in_1));  // open: en
  Multiplexer #(.select(4)) multiplexer_10 (
    .in0(in_2[9]), .in1(in_2[10]), .in2(in_2[11]), .in3(in_2[12]), .in4(in_2[13]), .in5(in_2[14]),
    .in6(in_2[15]), .in7(1'b0), .in8(1'b0), .in9(1'b0), .in10(1'b0), .in11(1'b0), .in12(1'b0), .in13(1'b0),
    .in14(1'b0), .in15(1'b0), .out(out_3[9]), .sel(in_1));  // open: en
  Multiplexer #(.select(4)) multiplexer_11 (
    .in0(in_2[10]), .in1(in_2[11]), .in2(in_2[12]), .in3(in_2[13]), .in4(in_2[14]), .in5(in_2[15]),
    .in6(1'b0), .in7(1'b0), .in8(1'b0), .in9(1'b0), .in10(1'b0), .in11(1'b0), .in12(1'b0), .in13(1'b0),
    .in14(1'b0), .in15(1'b0), .out(out_3[10]), .sel(in_1));  // open: en
  Multiplexer #(.select(4)) multiplexer_12 (
    .in0(in_2[11]), .in1(in_2[12]), .in2(in_2[13]), .in3(in_2[14]), .in4(in_2[15]), .in5(1'b0), .in6(1'b0),
    .in7(1'b0), .in8(1'b0), .in9(1'b0), .in10(1'b0), .in11(1'b0), .in12(1'b0), .in13(1'b0), .in14(1'b0),
    .in15(1'b0), .out(out_3[11]), .sel(in_1));  // open: en
  Multiplexer #(.select(4)) multiplexer_13 (
    .in0(in_2[12]), .in1(in_2[13]), .in2(in_2[14]), .in3(in_2[15]), .in4(1'b0), .in5(1'b0), .in6(1'b0),
    .in7(1'b0), .in8(1'b0), .in9(1'b0), .in10(1'b0), .in11(1'b0), .in12(1'b0), .in13(1'b0), .in14(1'b0),
    .in15(1'b0), .out(out_3[12]), .sel(in_1));  // open: en
  Multiplexer #(.select(4)) multiplexer_14 (
    .in0(in_2[13]), .in1(in_2[14]), .in2(in_2[15]), .in3(1'b0), .in4(1'b0), .in5(1'b0), .in6(1'b0),
    .in7(1'b0), .in8(1'b0), .in9(1'b0), .in10(1'b0), .in11(1'b0), .in12(1'b0), .in13(1'b0), .in14(1'b0),
    .in15(1'b0), .out(out_3[13]), .sel(in_1));  // open: en
  Multiplexer #(.select(4)) multiplexer_15 (
    .in0(in_2[14]), .in1(in_2[15]), .in2(1'b0), .in3(1'b0), .in4(1'b0), .in5(1'b0), .in6(1'b0), .in7(1'b0),
    .in8(1'b0), .in9(1'b0), .in10(1'b0), .in11(1'b0), .in12(1'b0), .in13(1'b0), .in14(1'b0), .in15(1'b0),
    .out(out_3[14]), .sel(in_1));  // open: en
  Multiplexer #(.select(4)) multiplexer_16 (
    .in0(in_2[15]), .in1(1'b0), .in2(1'b0), .in3(1'b0), .in4(1'b0), .in5(1'b0), .in6(1'b0), .in7(1'b0),
    .in8(1'b0), .in9(1'b0), .in10(1'b0), .in11(1'b0), .in12(1'b0), .in13(1'b0), .in14(1'b0), .in15(1'b0),
    .out(out_3[15]), .sel(in_1));  // open: en

  // Notes on the sheet:
  //   WAHEED UDDIN WAHEED
endmodule

module SLL (
  input  [15:0] in_1,
  input  [3:0] in_2,
  output [15:0] out_3
);

  Multiplexer #(.select(4)) multiplexer_1 (
    .in0(in_1[0]), .in1(1'b0), .in2(1'b0), .in3(1'b0), .in4(1'b0), .in5(1'b0), .in6(1'b0), .in7(1'b0),
    .in8(1'b0), .in9(1'b0), .in10(1'b0), .in11(1'b0), .in12(1'b0), .in13(1'b0), .in14(1'b0), .in15(1'b0),
    .out(out_3[0]), .sel(in_2));  // open: en
  Multiplexer #(.select(4)) multiplexer_2 (
    .in0(in_1[1]), .in1(in_1[0]), .in2(1'b0), .in3(1'b0), .in4(1'b0), .in5(1'b0), .in6(1'b0), .in7(1'b0),
    .in8(1'b0), .in9(1'b0), .in10(1'b0), .in11(1'b0), .in12(1'b0), .in13(1'b0), .in14(1'b0), .in15(1'b0),
    .out(out_3[1]), .sel(in_2));  // open: en
  Multiplexer #(.select(4)) multiplexer_3 (
    .in0(in_1[2]), .in1(in_1[1]), .in2(in_1[0]), .in3(1'b0), .in4(1'b0), .in5(1'b0), .in6(1'b0), .in7(1'b0),
    .in8(1'b0), .in9(1'b0), .in10(1'b0), .in11(1'b0), .in12(1'b0), .in13(1'b0), .in14(1'b0), .in15(1'b0),
    .out(out_3[2]), .sel(in_2));  // open: en
  Multiplexer #(.select(4)) multiplexer_4 (
    .in0(in_1[3]), .in1(in_1[2]), .in2(in_1[1]), .in3(in_1[0]), .in4(1'b0), .in5(1'b0), .in6(1'b0),
    .in7(1'b0), .in8(1'b0), .in9(1'b0), .in10(1'b0), .in11(1'b0), .in12(1'b0), .in13(1'b0), .in14(1'b0),
    .in15(1'b0), .out(out_3[3]), .sel(in_2));  // open: en
  Multiplexer #(.select(4)) multiplexer_5 (
    .in0(in_1[4]), .in1(in_1[3]), .in2(in_1[2]), .in3(in_1[1]), .in4(in_1[0]), .in5(1'b0), .in6(1'b0),
    .in7(1'b0), .in8(1'b0), .in9(1'b0), .in10(1'b0), .in11(1'b0), .in12(1'b0), .in13(1'b0), .in14(1'b0),
    .in15(1'b0), .out(out_3[4]), .sel(in_2));  // open: en
  Multiplexer #(.select(4)) multiplexer_6 (
    .in0(in_1[5]), .in1(in_1[4]), .in2(in_1[3]), .in3(in_1[2]), .in4(in_1[1]), .in5(in_1[0]), .in6(1'b0),
    .in7(1'b0), .in8(1'b0), .in9(1'b0), .in10(1'b0), .in11(1'b0), .in12(1'b0), .in13(1'b0), .in14(1'b0),
    .in15(1'b0), .out(out_3[5]), .sel(in_2));  // open: en
  Multiplexer #(.select(4)) multiplexer_7 (
    .in0(in_1[6]), .in1(in_1[5]), .in2(in_1[4]), .in3(in_1[3]), .in4(in_1[2]), .in5(in_1[1]), .in6(in_1[0]),
    .in7(1'b0), .in8(1'b0), .in9(1'b0), .in10(1'b0), .in11(1'b0), .in12(1'b0), .in13(1'b0), .in14(1'b0),
    .in15(1'b0), .out(out_3[6]), .sel(in_2));  // open: en
  Multiplexer #(.select(4)) multiplexer_8 (
    .in0(in_1[7]), .in1(in_1[6]), .in2(in_1[5]), .in3(in_1[4]), .in4(in_1[3]), .in5(in_1[2]), .in6(in_1[1]),
    .in7(in_1[0]), .in8(1'b0), .in9(1'b0), .in10(1'b0), .in11(1'b0), .in12(1'b0), .in13(1'b0), .in14(1'b0),
    .in15(1'b0), .out(out_3[7]), .sel(in_2));  // open: en
  Multiplexer #(.select(4)) multiplexer_9 (
    .in0(in_1[8]), .in1(in_1[7]), .in2(in_1[6]), .in3(in_1[5]), .in4(in_1[4]), .in5(in_1[3]), .in6(in_1[2]),
    .in7(in_1[1]), .in8(in_1[0]), .in9(1'b0), .in10(1'b0), .in11(1'b0), .in12(1'b0), .in13(1'b0),
    .in14(1'b0), .in15(1'b0), .out(out_3[8]), .sel(in_2));  // open: en
  Multiplexer #(.select(4)) multiplexer_10 (
    .in0(in_1[9]), .in1(in_1[8]), .in2(in_1[7]), .in3(in_1[6]), .in4(in_1[5]), .in5(in_1[4]), .in6(in_1[3]),
    .in7(in_1[2]), .in8(in_1[1]), .in9(in_1[0]), .in10(1'b0), .in11(1'b0), .in12(1'b0), .in13(1'b0),
    .in14(1'b0), .in15(1'b0), .out(out_3[9]), .sel(in_2));  // open: en
  Multiplexer #(.select(4)) multiplexer_11 (
    .in0(in_1[10]), .in1(in_1[9]), .in2(in_1[8]), .in3(in_1[7]), .in4(in_1[6]), .in5(in_1[5]), .in6(in_1[4]),
    .in7(in_1[3]), .in8(in_1[2]), .in9(in_1[1]), .in10(in_1[0]), .in11(1'b0), .in12(1'b0), .in13(1'b0),
    .in14(1'b0), .in15(1'b0), .out(out_3[10]), .sel(in_2));  // open: en
  Multiplexer #(.select(4)) multiplexer_12 (
    .in0(in_1[11]), .in1(in_1[10]), .in2(in_1[9]), .in3(in_1[8]), .in4(in_1[7]), .in5(in_1[6]),
    .in6(in_1[5]), .in7(in_1[4]), .in8(in_1[3]), .in9(in_1[2]), .in10(in_1[1]), .in11(in_1[0]), .in12(1'b0),
    .in13(1'b0), .in14(1'b0), .in15(1'b0), .out(out_3[11]), .sel(in_2));  // open: en
  Multiplexer #(.select(4)) multiplexer_13 (
    .in0(in_1[12]), .in1(in_1[11]), .in2(in_1[10]), .in3(in_1[9]), .in4(in_1[8]), .in5(in_1[7]),
    .in6(in_1[6]), .in7(in_1[5]), .in8(in_1[4]), .in9(in_1[3]), .in10(in_1[2]), .in11(in_1[1]),
    .in12(in_1[0]), .in13(1'b0), .in14(1'b0), .in15(1'b0), .out(out_3[12]), .sel(in_2));  // open: en
  Multiplexer #(.select(4)) multiplexer_14 (
    .in0(in_1[13]), .in1(in_1[12]), .in2(in_1[11]), .in3(in_1[10]), .in4(in_1[9]), .in5(in_1[8]),
    .in6(in_1[7]), .in7(in_1[6]), .in8(in_1[5]), .in9(in_1[4]), .in10(in_1[3]), .in11(in_1[2]),
    .in12(in_1[1]), .in13(in_1[0]), .in14(1'b0), .in15(1'b0), .out(out_3[13]), .sel(in_2));  // open: en
  Multiplexer #(.select(4)) multiplexer_15 (
    .in0(in_1[14]), .in1(in_1[13]), .in2(in_1[12]), .in3(in_1[11]), .in4(in_1[10]), .in5(in_1[9]),
    .in6(in_1[8]), .in7(in_1[7]), .in8(in_1[6]), .in9(in_1[5]), .in10(in_1[4]), .in11(in_1[3]),
    .in12(in_1[2]), .in13(in_1[1]), .in14(in_1[0]), .in15(1'b0), .out(out_3[14]), .sel(in_2));  // open: en
  Multiplexer #(.select(4)) multiplexer_16 (
    .in0(in_1[15]), .in1(in_1[14]), .in2(in_1[13]), .in3(in_1[12]), .in4(in_1[11]), .in5(in_1[10]),
    .in6(in_1[9]), .in7(in_1[8]), .in8(in_1[7]), .in9(in_1[6]), .in10(in_1[5]), .in11(in_1[4]),
    .in12(in_1[3]), .in13(in_1[2]), .in14(in_1[1]), .in15(in_1[0]), .out(out_3[15]), .sel(in_2));  // open: en

  // Notes on the sheet:
  //   WAHEED UDDIN WAHEED
endmodule

module Sign_Extention_16_bits (
  input  [3:0] in_1,
  output [15:0] out_2
);


  assign out_2 = {{13{in_1[3]}}, in_1[2:0]};

  // Notes on the sheet:
  //   WAHEED UDDIN WAHEED
endmodule

module Full_Data_Path (
  input  in_1,
  input  [3:0] OP,
  input  [3:0] RD,
  input  [3:0] RS,
  input  [3:0] RT,
  input  in_6,
  output [2:0] ALU_OP,
  output [3:0] OP_2,
  output [3:0] RD_2,
  output [3:0] RS_2,
  output [3:0] RT_2,
  output [15:0] Data_Out_1,
  output [15:0] Data_Out_2,
  output [15:0] RESULT
);

  wire alu_1_zero_flag, and_1_out, CLK_out, CLR_out, control_1_a_invert, control_1_alusrc,
       control_1_b_invert, control_1_branch, control_1_jump, control_1_memread, control_1_memtoreg,
       control_1_memwrite, control_1_reg_write, control_1_regdst, control_1_shift;
  wire [3:0] multiplexer_3_out, n16_bit_cla_1_out_put, n16_bit_cla_1_out_put_2, n16_bit_cla_1_out_put_3,
       n16_bit_cla_1_out_put_4, rom_1_data;
  wire [15:0] alu_1_result, multiplexer_2_out, multiplexer_4_out, multiplexer_6_out, n16_bit_cla_2_out_put,
       PC_q, ram_1_data, sign_extention_16_bits_1_out_2;

  Register #(.width(16)) PC (.D(multiplexer_6_out), .Q(PC_q), .clk(CLK_out), .clr(CLR_out));  // open: en
  _16_Bit_CLA u_16_bit_cla_1 (
    .Cin(in_1), .in_2(16'h1), .in_3(PC_q),
    .Out_put({n16_bit_cla_1_out_put, n16_bit_cla_1_out_put_4, n16_bit_cla_1_out_put_3, n16_bit_cla_1_out_put_2}));  // open: Cout
  Hex_Digit_Display hex_digit_display_1 (.value(OP_2));  // open: dp
  Button CLR (.out(CLR_out));
  Clock CLK (.out(CLK_out));
  Hex_Digit_Display hex_digit_display_2 (.value(RD_2));  // open: dp
  Hex_Digit_Display hex_digit_display_3 (.value(RS_2));  // open: dp
  Hex_Digit_Display hex_digit_display_4 (.value(rom_1_data));  // open: dp
  ROM #(.addrWidth(16), .dataWidth(16)) rom_1 (.addr(PC_q), .data({OP_2, RD_2, RS_2, rom_1_data}));  // open: sel
  Multiplexer #(.width(4)) multiplexer_1 (
    .in0(rom_1_data), .in1(RD_2), .out(RT_2), .sel(control_1_regdst));  // open: en
  Hex_Digit_Display hex_digit_display_5 (.value(OP));  // open: dp
  Hex_Digit_Display hex_digit_display_6 (.value(RS));  // open: dp
  Hex_Digit_Display hex_digit_display_7 (.value(RD));  // open: dp
  Register_File register_file_1 (
    .Clock(CLK_out), .Data_IN(RESULT), .RegWrite(control_1_reg_write), .Data01(Data_Out_1),
    .Data02(Data_Out_2), .RD(RD_2), .RS(RS_2), .RT(RT_2));
  Sign_Extention_16_bits sign_extention_16_bits_1 (.in_1(rom_1_data), .out_2(sign_extention_16_bits_1_out_2));
  Hex_Digit_Display hex_digit_display_8 (.value(RT));  // open: dp
  Multiplexer #(.width(16)) multiplexer_2 (
    .in0(Data_Out_2), .in1(sign_extention_16_bits_1_out_2), .out(multiplexer_2_out), .sel(control_1_alusrc));  // open: en
  Multiplexer #(.width(4)) multiplexer_3 (
    .in0(4'b0000), .in1(rom_1_data), .out(multiplexer_3_out), .sel(control_1_shift));  // open: en
  Control control_1 (
    .Op_Code(OP_2), .A_Invert(control_1_a_invert), .B_Invert(control_1_b_invert),
    .REG_Write(control_1_reg_write), .ALUSrc(control_1_alusrc), .REGdst(control_1_regdst),
    .MemToReg(control_1_memtoreg), .MemRead(control_1_memread), .MemWrite(control_1_memwrite),
    .Branch(control_1_branch), .ALU_OP(ALU_OP), .Shift(control_1_shift), .Jump(control_1_jump));
  ALU alu_1 (
    .Data_1(Data_Out_1), .Data_2(multiplexer_2_out), .A_invert(control_1_a_invert),
    .B_invert(control_1_b_invert), .Shift_Ammount(multiplexer_3_out), .Zero_Flag(alu_1_zero_flag),
    .Result(alu_1_result), .Cin(control_1_b_invert), .ALU_Op(ALU_OP));
  _16_Bit_CLA u_16_bit_cla_2 (
    .Cin(in_6),
    .in_2({n16_bit_cla_1_out_put, n16_bit_cla_1_out_put_4, n16_bit_cla_1_out_put_3, n16_bit_cla_1_out_put_2}),
    .in_3(sign_extention_16_bits_1_out_2), .Out_put(n16_bit_cla_2_out_put));  // open: Cout
  RAM #(.addrWidth(16), .dataWidth(16), .bus("separate")) ram_1 (
    .addr(alu_1_result), .din(Data_Out_2), .data(ram_1_data), .str(control_1_memwrite), .clk(CLK_out),
    .ld(control_1_memread));  // open: sel, clr
  Multiplexer #(.width(16)) multiplexer_4 (
    .in0({n16_bit_cla_1_out_put, n16_bit_cla_1_out_put_4, n16_bit_cla_1_out_put_3, n16_bit_cla_1_out_put_2}),
    .in1(n16_bit_cla_2_out_put), .out(multiplexer_4_out), .sel(and_1_out));  // open: en
  and and_1 (and_1_out, alu_1_zero_flag, control_1_branch);
  Multiplexer #(.width(16)) multiplexer_5 (
    .in0(alu_1_result), .in1(ram_1_data), .out(RESULT), .sel(control_1_memtoreg));  // open: en
  Multiplexer #(.width(16)) multiplexer_6 (
    .in0(multiplexer_4_out), .in1({n16_bit_cla_1_out_put, RD_2, RS_2, rom_1_data}), .out(multiplexer_6_out),
    .sel(control_1_jump));  // open: en

  // Notes on the sheet:
  //   ADD
  //   SUB
  //   contents of rom_1 (hex, n*v repeats v):
  //   8000 8101 8202 8303 8404 8505 8606 8707
  //   OR
  //   NOR
  //   AND
  //   INS CONVERTER
  //   XOR
  //   JUMP
  //   0000   0001   0010   0011   0100   0101   0110   0111   1000   1001   1010   1011   1100   1101   1110   1111
  //   ADDi
  //   MULT
  //   ASIF MAHMUD
  //   LW
  //   CURRENT OPERATIONS
  //   SW
  //   ORi
  //   ANDi
  //   SLL
  //   SRL
  //   BEQ
endmodule
